// Logisim project TD4.circ as structural Verilog: 18 circuits, main circuit main
module main (
  input  in_1,
  input  in_2,
  input  in_3,
  input  in_4
);

  wire clock_1_out, d_ff_1_q, decoder_td4_1_load_a, decoder_td4_1_load_b, decoder_td4_1_load_c,
       decoder_td4_1_load_d, decoder_td4_1_select_a, decoder_td4_1_select_b,
       fulladder4bit_1_c_out__carry_out, fulladder4bit_1_s0_out, fulladder4bit_1_s1_out,
       fulladder4bit_1_s2_out, fulladder4bit_1_s3_out, registories_1_a_out, registories_1_b_out,
       registories_1_c_out, registories_1_d_out, registories_1_led0, registories_1_led1, registories_1_led2,
       registories_1_led3, registories_1_prg_0, registories_1_prg_1, registories_1_prg_2,
       registories_1_prg_3, Reset_out, rom16byte_1_bit0, rom16byte_1_bit1, rom16byte_1_bit2,
       rom16byte_1_bit3, rom16byte_1_bit4, rom16byte_1_bit5, rom16byte_1_bit6, rom16byte_1_bit7;

  Decoder_TD4 decoder_td4_1 (
    .bit7(rom16byte_1_bit7), .bit6(rom16byte_1_bit6), .bit5(rom16byte_1_bit5), .bit4(rom16byte_1_bit4),
    .C_flag(d_ff_1_q), .LOAD_A(decoder_td4_1_load_a), .LOAD_B(decoder_td4_1_load_b),
    .LOAD_C(decoder_td4_1_load_c), .LOAD_D(decoder_td4_1_load_d), .SELECT_A(decoder_td4_1_select_a),
    .SELECT_B(decoder_td4_1_select_b));
  Clock clock_1 (.out(clock_1_out));
  Button Reset (.out(Reset_out));
  Registories registories_1 (
    .A_in(fulladder4bit_1_s0_out), .B_in(fulladder4bit_1_s1_out), .C_in(fulladder4bit_1_s2_out),
    .D_in(fulladder4bit_1_s3_out), .SELECT_A(decoder_td4_1_select_a), .SELECT_B(decoder_td4_1_select_b),
    .SW_0(in_1), .SW_1(in_2), .SW_2(in_3), .SW_3(in_4), .LoadD__When_0_load_input(decoder_td4_1_load_d),
    .LoadC__When_0_load_input(decoder_td4_1_load_c), .LoadB__When_0_load_input(decoder_td4_1_load_b),
    .LoadA__When_0_load_input(decoder_td4_1_load_a), .CLK(clock_1_out),
    .RST__When_1__clear_register(Reset_out), .PRG_3(registories_1_prg_3), .PRG_2(registories_1_prg_2),
    .PRG_1(registories_1_prg_1), .PRG_0(registories_1_prg_0), .LED0(registories_1_led0),
    .LED1(registories_1_led1), .LED2(registories_1_led2), .LED3(registories_1_led3),
    .A_out(registories_1_a_out), .B_out(registories_1_b_out), .C_out(registories_1_c_out),
    .D_out(registories_1_d_out));
  ROM16byte rom16byte_1 (
    .address0(registories_1_prg_0), .address1(registories_1_prg_1), .address2(registories_1_prg_2),
    .address3(registories_1_prg_3), .bit0(rom16byte_1_bit0), .bit1(rom16byte_1_bit1),
    .bit2(rom16byte_1_bit2), .bit3(rom16byte_1_bit3), .bit4(rom16byte_1_bit4), .bit5(rom16byte_1_bit5),
    .bit6(rom16byte_1_bit6), .bit7(rom16byte_1_bit7));
  LED led_1 (.in(registories_1_led0));
  LED led_2 (.in(registories_1_led1));
  LED led_3 (.in(registories_1_led2));
  LED led_4 (.in(registories_1_led3));
  FullAdder4bit fulladder4bit_1 (
    .Carry_in(1'b0), .A0_in(registories_1_a_out), .B0_in(rom16byte_1_bit0), .A1_in(registories_1_b_out),
    .B1_in(rom16byte_1_bit1), .A2_in(registories_1_c_out), .B2_in(rom16byte_1_bit2),
    .A3_in(registories_1_d_out), .B3_in(rom16byte_1_bit3), .S0_out(fulladder4bit_1_s0_out),
    .S1_out(fulladder4bit_1_s1_out), .S2_out(fulladder4bit_1_s2_out), .S3_out(fulladder4bit_1_s3_out),
    .C_out__Carry_out(fulladder4bit_1_c_out__carry_out));
  D_Flip_Flop d_ff_1 (
    .clk(clock_1_out), .D(fulladder4bit_1_c_out__carry_out), .Q(d_ff_1_q));  // open: Qn, preset, en, reset
endmodule

module HalfAdder (
  input  A_in,
  input  B_in,
  output S_out__Sum,
  output C_out__Carry_out
);

  xor xor_1 (S_out__Sum, A_in, B_in);
  and and_1 (C_out__Carry_out, A_in, B_in);
endmodule

module Counter4bit (
  input  CLK_in,
  input  RST__When_1__output_states_to_0,
  output T3_out,
  output T2_out,
  output T1_out,
  output T0_out
);

  wire HalfAdder_2_c_out__carry_out, HalfAdder_2_s_out__sum, HalfAdder_3_c_out__carry_out,
       HalfAdder_3_s_out__sum, HalfAdder_4_c_out__carry_out, HalfAdder_4_s_out__sum,
       HalfAdder_c_out__carry_out, HalfAdder_s_out__sum;

  HalfAdder HalfAdder (
    .A_in(T3_out), .B_in(HalfAdder_2_c_out__carry_out), .S_out__Sum(HalfAdder_s_out__sum),
    .C_out__Carry_out(HalfAdder_c_out__carry_out));
  HalfAdder HalfAdder_2 (
    .A_in(T2_out), .B_in(HalfAdder_3_c_out__carry_out), .S_out__Sum(HalfAdder_2_s_out__sum),
    .C_out__Carry_out(HalfAdder_2_c_out__carry_out));
  HalfAdder HalfAdder_3 (
    .A_in(T1_out), .B_in(HalfAdder_4_c_out__carry_out), .S_out__Sum(HalfAdder_3_s_out__sum),
    .C_out__Carry_out(HalfAdder_3_c_out__carry_out));
  HalfAdder HalfAdder_4 (
    .A_in(T0_out), .B_in(1'b1), .S_out__Sum(HalfAdder_4_s_out__sum),
    .C_out__Carry_out(HalfAdder_4_c_out__carry_out));
  D_Flip_Flop d_ff_1 (
    .clk(CLK_in), .D(HalfAdder_s_out__sum), .Q(T3_out), .reset(RST__When_1__output_states_to_0));  // open: Qn, preset, en
  D_Flip_Flop d_ff_2 (
    .clk(CLK_in), .D(HalfAdder_2_s_out__sum), .Q(T2_out), .reset(RST__When_1__output_states_to_0));  // open: Qn, preset, en
  D_Flip_Flop d_ff_3 (
    .clk(CLK_in), .D(HalfAdder_3_s_out__sum), .Q(T1_out), .reset(RST__When_1__output_states_to_0));  // open: Qn, preset, en
  D_Flip_Flop d_ff_4 (
    .clk(CLK_in), .D(HalfAdder_4_s_out__sum), .Q(T0_out), .reset(RST__When_1__output_states_to_0));  // open: Qn, preset, en
endmodule

module Counter8bit (
  input  CLK_in,
  input  RST__When_1__output_states_to_0,
  output T7_out,
  output T6_out,
  output T5_out,
  output T4_out,
  output T3_out,
  output T2_out,
  output T1_out,
  output T0_out
);

  wire HalfAdder_2_c_out__carry_out, HalfAdder_2_s_out__sum, HalfAdder_3_c_out__carry_out,
       HalfAdder_3_s_out__sum, HalfAdder_4_c_out__carry_out, HalfAdder_4_s_out__sum,
       HalfAdder_5_c_out__carry_out, HalfAdder_5_s_out__sum, HalfAdder_6_c_out__carry_out,
       HalfAdder_6_s_out__sum, HalfAdder_7_c_out__carry_out, HalfAdder_7_s_out__sum,
       HalfAdder_8_c_out__carry_out, HalfAdder_8_s_out__sum, HalfAdder_c_out__carry_out, HalfAdder_s_out__sum;

  HalfAdder HalfAdder (
    .A_in(T7_out), .B_in(HalfAdder_2_c_out__carry_out), .S_out__Sum(HalfAdder_s_out__sum),
    .C_out__Carry_out(HalfAdder_c_out__carry_out));
  HalfAdder HalfAdder_2 (
    .A_in(T6_out), .B_in(HalfAdder_3_c_out__carry_out), .S_out__Sum(HalfAdder_2_s_out__sum),
    .C_out__Carry_out(HalfAdder_2_c_out__carry_out));
  HalfAdder HalfAdder_3 (
    .A_in(T5_out), .B_in(HalfAdder_4_c_out__carry_out), .S_out__Sum(HalfAdder_3_s_out__sum),
    .C_out__Carry_out(HalfAdder_3_c_out__carry_out));
  HalfAdder HalfAdder_4 (
    .A_in(T4_out), .B_in(HalfAdder_5_c_out__carry_out), .S_out__Sum(HalfAdder_4_s_out__sum),
    .C_out__Carry_out(HalfAdder_4_c_out__carry_out));
  HalfAdder HalfAdder_5 (
    .A_in(T3_out), .B_in(HalfAdder_6_c_out__carry_out), .S_out__Sum(HalfAdder_5_s_out__sum),
    .C_out__Carry_out(HalfAdder_5_c_out__carry_out));
  HalfAdder HalfAdder_6 (
    .A_in(T2_out), .B_in(HalfAdder_7_c_out__carry_out), .S_out__Sum(HalfAdder_6_s_out__sum),
    .C_out__Carry_out(HalfAdder_6_c_out__carry_out));
  HalfAdder HalfAdder_7 (
    .A_in(T1_out), .B_in(HalfAdder_8_c_out__carry_out), .S_out__Sum(HalfAdder_7_s_out__sum),
    .C_out__Carry_out(HalfAdder_7_c_out__carry_out));
  HalfAdder HalfAdder_8 (
    .A_in(T0_out), .B_in(1'b1), .S_out__Sum(HalfAdder_8_s_out__sum),
    .C_out__Carry_out(HalfAdder_8_c_out__carry_out));
  D_Flip_Flop d_ff_1 (
    .clk(CLK_in), .D(HalfAdder_s_out__sum), .Q(T7_out), .reset(RST__When_1__output_states_to_0));  // open: Qn, preset, en
  D_Flip_Flop d_ff_2 (
    .clk(CLK_in), .D(HalfAdder_2_s_out__sum), .Q(T6_out), .reset(RST__When_1__output_states_to_0));  // open: Qn, preset, en
  D_Flip_Flop d_ff_3 (
    .clk(CLK_in), .D(HalfAdder_3_s_out__sum), .Q(T5_out), .reset(RST__When_1__output_states_to_0));  // open: Qn, preset, en
  D_Flip_Flop d_ff_4 (
    .clk(CLK_in), .D(HalfAdder_4_s_out__sum), .Q(T4_out), .reset(RST__When_1__output_states_to_0));  // open: Qn, preset, en
  D_Flip_Flop d_ff_5 (
    .clk(CLK_in), .D(HalfAdder_5_s_out__sum), .Q(T3_out), .reset(RST__When_1__output_states_to_0));  // open: Qn, preset, en
  D_Flip_Flop d_ff_6 (
    .clk(CLK_in), .D(HalfAdder_6_s_out__sum), .Q(T2_out), .reset(RST__When_1__output_states_to_0));  // open: Qn, preset, en
  D_Flip_Flop d_ff_7 (
    .clk(CLK_in), .D(HalfAdder_7_s_out__sum), .Q(T1_out), .reset(RST__When_1__output_states_to_0));  // open: Qn, preset, en
  D_Flip_Flop d_ff_8 (
    .clk(CLK_in), .D(HalfAdder_8_s_out__sum), .Q(T0_out), .reset(RST__When_1__output_states_to_0));  // open: Qn, preset, en
endmodule

module FullAdder (
  input  A_in,
  input  B_in,
  input  C_in,
  output S_out__Sum,
  output C_out__Carry_out
);

  wire HalfAdder_2_c_out__carry_out, HalfAdder_c_out__carry_out, HalfAdder_s_out__sum;

  HalfAdder HalfAdder (
    .A_in(A_in), .B_in(B_in), .S_out__Sum(HalfAdder_s_out__sum), .C_out__Carry_out(HalfAdder_c_out__carry_out));
  HalfAdder HalfAdder_2 (
    .A_in(HalfAdder_s_out__sum), .B_in(C_in), .S_out__Sum(S_out__Sum),
    .C_out__Carry_out(HalfAdder_2_c_out__carry_out));
  or or_1 (C_out__Carry_out, HalfAdder_c_out__carry_out, HalfAdder_2_c_out__carry_out);
endmodule

// REG4
module Register4bit (
  input  RST__When_1__outputs_are_0,
  input  CLK,
  input  LD__When_0_load_input,
  input  A_in,
  input  B_in,
  input  C_in,
  input  D_in,
  output QA_out,
  output QB_out,
  output QC_out,
  output QD_out
);

  wire and_1_out, and_2_out, and_3_out, and_4_out, and_5_out, and_6_out, and_7_out, and_8_out, not_1_out,
       or_1_out, or_2_out, or_3_out, or_4_out;

  not not_1 (not_1_out, LD__When_0_load_input);
  and and_1 (and_1_out, QA_out, LD__When_0_load_input);
  and and_2 (and_2_out, A_in, not_1_out);
  and and_3 (and_3_out, QB_out, LD__When_0_load_input);
  and and_4 (and_4_out, B_in, not_1_out);
  and and_5 (and_5_out, QC_out, LD__When_0_load_input);
  and and_6 (and_6_out, C_in, not_1_out);
  and and_7 (and_7_out, QD_out, LD__When_0_load_input);
  and and_8 (and_8_out, D_in, not_1_out);
  or or_1 (or_1_out, and_1_out, and_2_out);
  or or_2 (or_2_out, and_3_out, and_4_out);
  or or_3 (or_3_out, and_5_out, and_6_out);
  or or_4 (or_4_out, and_7_out, and_8_out);
  D_Flip_Flop d_ff_1 (.clk(CLK), .D(or_1_out), .Q(QA_out), .reset(RST__When_1__outputs_are_0));  // open: Qn, preset, en
  D_Flip_Flop d_ff_2 (.clk(CLK), .D(or_2_out), .Q(QB_out), .reset(RST__When_1__outputs_are_0));  // open: Qn, preset, en
  D_Flip_Flop d_ff_3 (.clk(CLK), .D(or_3_out), .Q(QC_out), .reset(RST__When_1__outputs_are_0));  // open: Qn, preset, en
  D_Flip_Flop d_ff_4 (.clk(CLK), .D(or_4_out), .Q(QD_out), .reset(RST__When_1__outputs_are_0));  // open: Qn, preset, en

  // Notes on the sheet:
  //   LDがLでロード,Hで保持
  //   タイマーなし74HC161みたいなやつ(P185)
endmodule

// SLCT4
module Selecter4bit (
  input  SELECT_A,
  input  SELECT_B,
  input  C0_in,
  input  C1_in,
  input  C2_in,
  input  C3_in,
  output C_out
);

  wire and_1_out, and_2_out, and_3_out, and_4_out, not_1_out, not_2_out;

  not not_1 (not_1_out, SELECT_B);
  not not_2 (not_2_out, SELECT_A);
  and and_1 (and_1_out, C0_in, not_2_out, not_1_out);
  and and_2 (and_2_out, C1_in, SELECT_A, not_1_out);
  and and_3 (and_3_out, C2_in, not_2_out, SELECT_B);
  and and_4 (and_4_out, C3_in, SELECT_A, SELECT_B);
  or or_1 (C_out, and_1_out, and_2_out, and_3_out, and_4_out);

  // Notes on the sheet:
  //   データセレクタ 74HC153っぽいの(P176)
  //   SELECT B,Aについて，B*2+Aが出力される
endmodule

module Selecter8bit (
  input  SELECT_A,
  input  SELECT_B,
  input  SELECT_C,
  input  C0_in,
  input  C1_in,
  input  C2_in,
  input  C3_in,
  input  C4_in,
  input  C5_in,
  input  C6_in,
  input  C7_in,
  output out_12
);

  wire and_1_out, and_2_out, not_1_out, SLCT4_2_c_out, SLCT4_c_out;

  Selecter4bit SLCT4 (
    .SELECT_A(SELECT_A), .SELECT_B(SELECT_B), .C0_in(C0_in), .C1_in(C1_in), .C2_in(C2_in), .C3_in(C3_in),
    .C_out(SLCT4_c_out));
  Selecter4bit SLCT4_2 (
    .SELECT_A(SELECT_A), .SELECT_B(SELECT_B), .C0_in(C4_in), .C1_in(C5_in), .C2_in(C6_in), .C3_in(C7_in),
    .C_out(SLCT4_2_c_out));
  not not_1 (not_1_out, SELECT_C);
  and and_1 (and_1_out, SLCT4_c_out, not_1_out);
  and and_2 (and_2_out, SLCT4_2_c_out, SELECT_C);
  or or_1 (out_12, and_1_out, and_2_out);
endmodule

module FullAdder8bit (
  input  Carry_in,
  input  A0_in,
  input  B0_in,
  input  A1_in,
  input  B1_in,
  input  A2_in,
  input  B2_in,
  input  A3_in,
  input  B3_in,
  input  A4_in,
  input  B4_in,
  input  A5_in,
  input  B5_in,
  input  A6_in,
  input  B6_in,
  input  A7_in,
  input  B7_in,
  output S0_out,
  output S1_out,
  output S2_out,
  output S3_out,
  output S4_out,
  output S5_out,
  output S6_out,
  output S7_out,
  output C_out__Carry_out
);

  wire FA4_c_out__carry_out;

  FullAdder4bit FA4 (
    .Carry_in(Carry_in), .A0_in(A0_in), .B0_in(B0_in), .A1_in(A1_in), .B1_in(B1_in), .A2_in(A2_in),
    .B2_in(B2_in), .A3_in(A3_in), .B3_in(B3_in), .S0_out(S0_out), .S1_out(S1_out), .S2_out(S2_out),
    .S3_out(S3_out), .C_out__Carry_out(FA4_c_out__carry_out));
  FullAdder4bit FA4_2 (
    .Carry_in(FA4_c_out__carry_out), .A0_in(A4_in), .B0_in(B4_in), .A1_in(A5_in), .B1_in(B5_in),
    .A2_in(A6_in), .B2_in(B6_in), .A3_in(A7_in), .B3_in(B7_in), .S0_out(S4_out), .S1_out(S5_out),
    .S2_out(S6_out), .S3_out(S7_out), .C_out__Carry_out(C_out__Carry_out));
endmodule

// FA4
module FullAdder4bit (
  input  Carry_in,
  input  A0_in,
  input  B0_in,
  input  A1_in,
  input  B1_in,
  input  A2_in,
  input  B2_in,
  input  A3_in,
  input  B3_in,
  output S0_out,
  output S1_out,
  output S2_out,
  output S3_out,
  output C_out__Carry_out
);

  wire FA_2_c_out__carry_out, FA_3_c_out__carry_out, FA_c_out__carry_out;

  FullAdder FA (
    .A_in(Carry_in), .B_in(A0_in), .C_in(B0_in), .S_out__Sum(S0_out), .C_out__Carry_out(FA_c_out__carry_out));
  FullAdder FA_2 (
    .A_in(FA_c_out__carry_out), .B_in(A1_in), .C_in(B1_in), .S_out__Sum(S1_out),
    .C_out__Carry_out(FA_2_c_out__carry_out));
  FullAdder FA_3 (
    .A_in(FA_2_c_out__carry_out), .B_in(A2_in), .C_in(B2_in), .S_out__Sum(S2_out),
    .C_out__Carry_out(FA_3_c_out__carry_out));
  FullAdder FA_4 (
    .A_in(FA_3_c_out__carry_out), .B_in(A3_in), .C_in(B3_in), .S_out__Sum(S3_out),
    .C_out__Carry_out(C_out__Carry_out));
endmodule

module Register8bit (
  input  RST__When_1__outputs_are_0,
  input  CLK,
  input  LD__When_0_load_input,
  input  A_in,
  input  B_in,
  input  C_in,
  input  D_in,
  input  E_in,
  input  F_in,
  input  G_in,
  input  H_in,
  output QA_out,
  output QB_out,
  output QC_out,
  output QD_out,
  output QE_out,
  output QF_out,
  output QG_out,
  output QH_out
);

  Register4bit register4bit_1 (
    .RST__When_1__outputs_are_0(RST__When_1__outputs_are_0), .CLK(CLK),
    .LD__When_0_load_input(LD__When_0_load_input), .A_in(A_in), .B_in(B_in), .C_in(C_in), .D_in(D_in),
    .QA_out(QA_out), .QB_out(QB_out), .QC_out(QC_out), .QD_out(QD_out));
  Register4bit register4bit_2 (
    .RST__When_1__outputs_are_0(RST__When_1__outputs_are_0), .CLK(CLK),
    .LD__When_0_load_input(LD__When_0_load_input), .A_in(E_in), .B_in(F_in), .C_in(G_in), .D_in(H_in),
    .QA_out(QE_out), .QB_out(QF_out), .QC_out(QG_out), .QD_out(QH_out));
endmodule

module ROM16byte (
  input  address0,
  input  address1,
  input  address2,
  input  address3,
  output bit0,
  output bit1,
  output bit2,
  output bit3,
  output bit4,
  output bit5,
  output bit6,
  output bit7
);

  wire _0x00_out, _0x0A_out, _0x0B_out, _0x0C_out, _0x0D_out, _0x0E_out, _0x0F_out, _0x01_out, _0x02_out,
       _0x03_out, _0x04_out, _0x05_out, _0x06_out, _0x07_out, _0x08_out, _0x09_out, and_1_out, and_2_out,
       and_3_out, and_4_out, and_5_out, and_6_out, and_7_out, and_8_out, and_9_out, and_10_out, and_11_out,
       and_12_out, and_13_out, and_14_out, and_15_out, and_16_out, and_17_out, and_18_out, and_19_out,
       and_20_out, and_21_out, and_22_out, and_23_out, and_24_out, and_25_out, and_26_out, and_27_out,
       and_28_out, and_29_out, and_30_out, and_31_out, and_32_out, and_33_out, and_34_out, and_35_out,
       and_36_out, and_37_out, and_38_out, and_39_out, and_40_out, and_41_out, and_42_out, and_43_out,
       and_44_out, and_45_out, and_46_out, and_47_out, and_48_out, and_49_out, and_50_out, and_51_out,
       and_52_out, and_53_out, and_54_out, and_55_out, and_56_out, and_57_out, and_58_out, and_59_out,
       and_60_out, and_61_out, and_62_out, and_63_out, and_64_out, and_65_out, and_66_out, and_67_out,
       and_68_out, and_69_out, and_70_out, and_71_out, and_72_out, and_73_out, and_74_out, and_75_out,
       and_76_out, and_77_out, and_78_out, and_79_out, and_80_out, and_81_out, and_82_out, and_83_out,
       and_84_out, and_85_out, and_86_out, and_87_out, and_88_out, and_89_out, and_90_out, and_91_out,
       and_92_out, and_93_out, and_94_out, and_95_out, and_96_out, and_97_out, and_98_out, and_99_out,
       and_100_out, and_101_out, and_102_out, and_103_out, and_104_out, and_105_out, and_106_out,
       and_107_out, and_108_out, and_109_out, and_110_out, and_111_out, and_112_out, and_113_out,
       and_114_out, and_115_out, and_116_out, and_117_out, and_118_out, and_119_out, and_120_out,
       and_121_out, and_122_out, and_123_out, and_124_out, and_125_out, and_126_out, and_127_out,
       and_128_out, marge8bit_1_a_out, marge8bit_1_b_out, marge8bit_1_c_out, marge8bit_1_d_out,
       marge8bit_1_e_out, marge8bit_1_f_out, marge8bit_1_g_out, marge8bit_1_h_out, marge8bit_2_a_out,
       marge8bit_2_b_out, marge8bit_2_c_out, marge8bit_2_d_out, marge8bit_2_e_out, marge8bit_2_f_out,
       marge8bit_2_g_out, marge8bit_2_h_out, marge8bit_3_a_out, marge8bit_3_b_out, marge8bit_3_c_out,
       marge8bit_3_d_out, marge8bit_3_e_out, marge8bit_3_f_out, marge8bit_3_g_out, marge8bit_3_h_out,
       marge8bit_4_a_out, marge8bit_4_b_out, marge8bit_4_c_out, marge8bit_4_d_out, marge8bit_4_e_out,
       marge8bit_4_f_out, marge8bit_4_g_out, marge8bit_4_h_out, marge8bit_5_a_out, marge8bit_5_b_out,
       marge8bit_5_c_out, marge8bit_5_d_out, marge8bit_5_e_out, marge8bit_5_f_out, marge8bit_5_g_out,
       marge8bit_5_h_out, marge8bit_6_a_out, marge8bit_6_b_out, marge8bit_6_c_out, marge8bit_6_d_out,
       marge8bit_6_e_out, marge8bit_6_f_out, marge8bit_6_g_out, marge8bit_6_h_out, marge8bit_7_a_out,
       marge8bit_7_b_out, marge8bit_7_c_out, marge8bit_7_d_out, marge8bit_7_e_out, marge8bit_7_f_out,
       marge8bit_7_g_out, marge8bit_7_h_out, marge8bit_8_a_out, marge8bit_8_b_out, marge8bit_8_c_out,
       marge8bit_8_d_out, marge8bit_8_e_out, marge8bit_8_f_out, marge8bit_8_g_out, marge8bit_8_h_out,
       marge8bit_9_a_out, marge8bit_9_b_out, marge8bit_9_c_out, marge8bit_9_d_out, marge8bit_9_e_out,
       marge8bit_9_f_out, marge8bit_9_g_out, marge8bit_9_h_out, marge8bit_10_a_out, marge8bit_10_b_out,
       marge8bit_10_c_out, marge8bit_10_d_out, marge8bit_10_e_out, marge8bit_10_f_out, marge8bit_10_g_out,
       marge8bit_10_h_out, marge8bit_11_a_out, marge8bit_11_b_out, marge8bit_11_c_out, marge8bit_11_d_out,
       marge8bit_11_e_out, marge8bit_11_f_out, marge8bit_11_g_out, marge8bit_11_h_out, marge8bit_12_a_out,
       marge8bit_12_b_out, marge8bit_12_c_out, marge8bit_12_d_out, marge8bit_12_e_out, marge8bit_12_f_out,
       marge8bit_12_g_out, marge8bit_12_h_out, marge8bit_13_a_out, marge8bit_13_b_out, marge8bit_13_c_out,
       marge8bit_13_d_out, marge8bit_13_e_out, marge8bit_13_f_out, marge8bit_13_g_out, marge8bit_13_h_out,
       marge8bit_14_a_out, marge8bit_14_b_out, marge8bit_14_c_out, marge8bit_14_d_out, marge8bit_14_e_out,
       marge8bit_14_f_out, marge8bit_14_g_out, marge8bit_14_h_out, marge8bit_15_a_out, marge8bit_15_b_out,
       marge8bit_15_c_out, marge8bit_15_d_out, marge8bit_15_e_out, marge8bit_15_f_out, marge8bit_15_g_out,
       marge8bit_15_h_out, not_1_out, not_2_out, not_3_out, not_4_out;

  not not_1 (not_1_out, address1);
  not not_2 (not_2_out, address2);
  not not_3 (not_3_out, address3);
  and and_1 (and_1_out, _0x00_out, 1'b0);
  and and_2 (and_2_out, _0x01_out, 1'b1);
  and and_3 (and_3_out, _0x02_out, 1'b0);
  and and_4 (and_4_out, _0x03_out, 1'b1);
  and and_5 (and_5_out, _0x04_out, 1'b1);
  and and_6 (and_6_out, _0x05_out, 1'b1);
  and and_7 (and_7_out, _0x06_out, 1'b1);
  and and_8 (and_8_out, _0x07_out, 1'b0);
  and and_9 (and_9_out, _0x08_out, 1'b0);
  and and_10 (and_10_out, _0x09_out, 1'b0);
  and and_11 (and_11_out, _0x0A_out, 1'b0);
  and and_12 (and_12_out, _0x0B_out, 1'b0);
  and and_13 (and_13_out, _0x0C_out, 1'b0);
  and and_14 (and_14_out, _0x0D_out, 1'b0);
  and and_15 (and_15_out, _0x0E_out, 1'b0);
  and and_16 (and_16_out, _0x0F_out, 1'b0);
  not not_4 (not_4_out, address0);
  and _0x00 (_0x00_out, not_4_out, not_1_out, not_2_out, not_3_out);
  and and_17 (and_17_out, _0x00_out, 1'b0);
  and and_18 (and_18_out, _0x00_out, 1'b1);
  and _0x01 (_0x01_out, not_1_out, not_2_out, not_3_out, address0);
  and and_19 (and_19_out, _0x01_out, 1'b0);
  and and_20 (and_20_out, _0x01_out, 1'b0);
  and _0x02 (_0x02_out, not_4_out, not_2_out, not_3_out, address1);
  and and_21 (and_21_out, _0x02_out, 1'b0);
  and and_22 (and_22_out, _0x02_out, 1'b0);
  and _0x03 (_0x03_out, not_2_out, not_3_out, address0, address1);
  and and_23 (and_23_out, _0x03_out, 1'b1);
  and and_24 (and_24_out, _0x03_out, 1'b1);
  and _0x04 (_0x04_out, not_4_out, not_1_out, not_3_out, address2);
  and and_25 (and_25_out, _0x04_out, 1'b1);
  and and_26 (and_26_out, _0x04_out, 1'b0);
  and _0x05 (_0x05_out, not_1_out, not_3_out, address0, address2);
  and and_27 (and_27_out, _0x05_out, 1'b1);
  and and_28 (and_28_out, _0x05_out, 1'b0);
  and _0x06 (_0x06_out, not_4_out, not_3_out, address1, address2);
  and and_29 (and_29_out, _0x06_out, 1'b1);
  and and_30 (and_30_out, _0x06_out, 1'b1);
  and _0x07 (_0x07_out, not_3_out, address0, address1, address2);
  and and_31 (and_31_out, _0x07_out, 1'b0);
  and and_32 (and_32_out, _0x07_out, 1'b0);
  and _0x08 (_0x08_out, not_4_out, not_1_out, not_2_out, address3);
  and and_33 (and_33_out, _0x08_out, 1'b0);
  and and_34 (and_34_out, _0x08_out, 1'b0);
  and _0x09 (_0x09_out, not_1_out, not_2_out, address0, address3);
  and and_35 (and_35_out, _0x09_out, 1'b0);
  and and_36 (and_36_out, _0x09_out, 1'b0);
  and _0x0A (_0x0A_out, not_4_out, not_2_out, address1, address3);
  and and_37 (and_37_out, _0x0A_out, 1'b0);
  and and_38 (and_38_out, _0x0A_out, 1'b0);
  and _0x0B (_0x0B_out, not_2_out, address0, address1, address3);
  and and_39 (and_39_out, _0x0B_out, 1'b0);
  and and_40 (and_40_out, _0x0B_out, 1'b0);
  and _0x0C (_0x0C_out, not_4_out, not_1_out, address2, address3);
  and and_41 (and_41_out, _0x0C_out, 1'b0);
  and and_42 (and_42_out, _0x0C_out, 1'b0);
  and _0x0D (_0x0D_out, not_1_out, address0, address2, address3);
  and and_43 (and_43_out, _0x0D_out, 1'b0);
  and and_44 (and_44_out, _0x0D_out, 1'b0);
  and _0x0E (_0x0E_out, not_4_out, address1, address2, address3);
  and and_45 (and_45_out, _0x0E_out, 1'b0);
  and and_46 (and_46_out, _0x0E_out, 1'b0);
  and _0x0F (_0x0F_out, address0, address1, address2, address3);
  and and_47 (and_47_out, _0x0F_out, 1'b0);
  and and_48 (and_48_out, _0x0F_out, 1'b0);
  and and_49 (and_49_out, _0x00_out, 1'b0);
  and and_50 (and_50_out, _0x00_out, 1'b0);
  and and_51 (and_51_out, _0x01_out, 1'b1);
  and and_52 (and_52_out, _0x01_out, 1'b0);
  and and_53 (and_53_out, _0x02_out, 1'b0);
  and and_54 (and_54_out, _0x02_out, 1'b0);
  and and_55 (and_55_out, _0x03_out, 1'b0);
  and and_56 (and_56_out, _0x03_out, 1'b0);
  and and_57 (and_57_out, _0x04_out, 1'b1);
  and and_58 (and_58_out, _0x04_out, 1'b1);
  and and_59 (and_59_out, _0x05_out, 1'b0);
  and and_60 (and_60_out, _0x05_out, 1'b1);
  and and_61 (and_61_out, _0x06_out, 1'b1);
  and and_62 (and_62_out, _0x06_out, 1'b0);
  and and_63 (and_63_out, _0x07_out, 1'b0);
  and and_64 (and_64_out, _0x07_out, 1'b0);
  and and_65 (and_65_out, _0x08_out, 1'b0);
  and and_66 (and_66_out, _0x08_out, 1'b0);
  and and_67 (and_67_out, _0x09_out, 1'b0);
  and and_68 (and_68_out, _0x09_out, 1'b0);
  and and_69 (and_69_out, _0x0A_out, 1'b0);
  and and_70 (and_70_out, _0x0A_out, 1'b0);
  and and_71 (and_71_out, _0x0B_out, 1'b0);
  and and_72 (and_72_out, _0x0B_out, 1'b0);
  and and_73 (and_73_out, _0x0C_out, 1'b0);
  and and_74 (and_74_out, _0x0C_out, 1'b0);
  and and_75 (and_75_out, _0x0D_out, 1'b0);
  and and_76 (and_76_out, _0x0D_out, 1'b0);
  and and_77 (and_77_out, _0x0E_out, 1'b0);
  and and_78 (and_78_out, _0x0E_out, 1'b0);
  and and_79 (and_79_out, _0x0F_out, 1'b0);
  and and_80 (and_80_out, _0x0F_out, 1'b0);
  and and_81 (and_81_out, _0x00_out, 1'b0);
  and and_82 (and_82_out, _0x00_out, 1'b0);
  and and_83 (and_83_out, _0x01_out, 1'b0);
  and and_84 (and_84_out, _0x01_out, 1'b0);
  and and_85 (and_85_out, _0x02_out, 1'b0);
  and and_86 (and_86_out, _0x02_out, 1'b0);
  and and_87 (and_87_out, _0x03_out, 1'b0);
  and and_88 (and_88_out, _0x03_out, 1'b0);
  and and_89 (and_89_out, _0x04_out, 1'b1);
  and and_90 (and_90_out, _0x04_out, 1'b1);
  and and_91 (and_91_out, _0x05_out, 1'b0);
  and and_92 (and_92_out, _0x05_out, 1'b0);
  and and_93 (and_93_out, _0x06_out, 1'b0);
  and and_94 (and_94_out, _0x06_out, 1'b1);
  and and_95 (and_95_out, _0x07_out, 1'b0);
  and and_96 (and_96_out, _0x07_out, 1'b0);
  and and_97 (and_97_out, _0x08_out, 1'b0);
  and and_98 (and_98_out, _0x08_out, 1'b0);
  and and_99 (and_99_out, _0x09_out, 1'b0);
  and and_100 (and_100_out, _0x09_out, 1'b0);
  and and_101 (and_101_out, _0x0A_out, 1'b0);
  and and_102 (and_102_out, _0x0A_out, 1'b0);
  and and_103 (and_103_out, _0x0B_out, 1'b0);
  and and_104 (and_104_out, _0x0B_out, 1'b0);
  and and_105 (and_105_out, _0x0C_out, 1'b0);
  and and_106 (and_106_out, _0x0C_out, 1'b0);
  and and_107 (and_107_out, _0x0D_out, 1'b0);
  and and_108 (and_108_out, _0x0D_out, 1'b0);
  and and_109 (and_109_out, _0x0E_out, 1'b0);
  and and_110 (and_110_out, _0x0E_out, 1'b0);
  and and_111 (and_111_out, _0x0F_out, 1'b0);
  and and_112 (and_112_out, _0x0F_out, 1'b0);
  and and_113 (and_113_out, _0x00_out, 1'b0);
  Marge8bit marge8bit_1 (
    .A0(and_113_out), .B0(and_81_out), .C0(and_82_out), .D0(and_49_out), .E0(and_50_out), .F0(and_17_out),
    .G0(and_18_out), .H0(and_1_out), .A1(1'b0), .B1(1'b0), .C1(1'b0), .D1(1'b0), .E1(1'b0), .F1(1'b0),
    .G1(1'b0), .H1(1'b0), .A_out(marge8bit_1_a_out), .B_out(marge8bit_1_b_out), .C_out(marge8bit_1_c_out),
    .D_out(marge8bit_1_d_out), .E_out(marge8bit_1_e_out), .F_out(marge8bit_1_f_out),
    .G_out(marge8bit_1_g_out), .H_out(marge8bit_1_h_out));
  and and_114 (and_114_out, _0x01_out, 1'b0);
  Marge8bit marge8bit_2 (
    .A0(and_114_out), .B0(and_84_out), .C0(and_83_out), .D0(and_52_out), .E0(and_51_out), .F0(and_19_out),
    .G0(and_20_out), .H0(and_2_out), .A1(marge8bit_1_a_out), .B1(marge8bit_1_b_out), .C1(marge8bit_1_c_out),
    .D1(marge8bit_1_d_out), .E1(marge8bit_1_e_out), .F1(marge8bit_1_f_out), .G1(marge8bit_1_g_out),
    .H1(marge8bit_1_h_out), .A_out(marge8bit_2_a_out), .B_out(marge8bit_2_b_out), .C_out(marge8bit_2_c_out),
    .D_out(marge8bit_2_d_out), .E_out(marge8bit_2_e_out), .F_out(marge8bit_2_f_out),
    .G_out(marge8bit_2_g_out), .H_out(marge8bit_2_h_out));
  and and_115 (and_115_out, _0x02_out, 1'b1);
  Marge8bit marge8bit_3 (
    .A0(and_115_out), .B0(and_85_out), .C0(and_86_out), .D0(and_54_out), .E0(and_53_out), .F0(and_22_out),
    .G0(and_21_out), .H0(and_3_out), .A1(marge8bit_2_a_out), .B1(marge8bit_2_b_out), .C1(marge8bit_2_c_out),
    .D1(marge8bit_2_d_out), .E1(marge8bit_2_e_out), .F1(marge8bit_2_f_out), .G1(marge8bit_2_g_out),
    .H1(marge8bit_2_h_out), .A_out(marge8bit_3_a_out), .B_out(marge8bit_3_b_out), .C_out(marge8bit_3_c_out),
    .D_out(marge8bit_3_d_out), .E_out(marge8bit_3_e_out), .F_out(marge8bit_3_f_out),
    .G_out(marge8bit_3_g_out), .H_out(marge8bit_3_h_out));
  and and_116 (and_116_out, _0x03_out, 1'b0);
  Marge8bit marge8bit_4 (
    .A0(and_116_out), .B0(and_87_out), .C0(and_88_out), .D0(and_55_out), .E0(and_56_out), .F0(and_23_out),
    .G0(and_24_out), .H0(and_4_out), .A1(marge8bit_3_a_out), .B1(marge8bit_3_b_out), .C1(marge8bit_3_c_out),
    .D1(marge8bit_3_d_out), .E1(marge8bit_3_e_out), .F1(marge8bit_3_f_out), .G1(marge8bit_3_g_out),
    .H1(marge8bit_3_h_out), .A_out(marge8bit_4_a_out), .B_out(marge8bit_4_b_out), .C_out(marge8bit_4_c_out),
    .D_out(marge8bit_4_d_out), .E_out(marge8bit_4_e_out), .F_out(marge8bit_4_f_out),
    .G_out(marge8bit_4_g_out), .H_out(marge8bit_4_h_out));
  and and_117 (and_117_out, _0x04_out, 1'b1);
  Marge8bit marge8bit_5 (
    .A0(and_117_out), .B0(and_90_out), .C0(and_89_out), .D0(and_58_out), .E0(and_57_out), .F0(and_25_out),
    .G0(and_26_out), .H0(and_5_out), .A1(marge8bit_4_a_out), .B1(marge8bit_4_b_out), .C1(marge8bit_4_c_out),
    .D1(marge8bit_4_d_out), .E1(marge8bit_4_e_out), .F1(marge8bit_4_f_out), .G1(marge8bit_4_g_out),
    .H1(marge8bit_4_h_out), .A_out(marge8bit_5_a_out), .B_out(marge8bit_5_b_out), .C_out(marge8bit_5_c_out),
    .D_out(marge8bit_5_d_out), .E_out(marge8bit_5_e_out), .F_out(marge8bit_5_f_out),
    .G_out(marge8bit_5_g_out), .H_out(marge8bit_5_h_out));
  and and_118 (and_118_out, _0x05_out, 1'b0);
  Marge8bit marge8bit_6 (
    .A0(and_118_out), .B0(and_92_out), .C0(and_91_out), .D0(and_59_out), .E0(and_60_out), .F0(and_27_out),
    .G0(and_28_out), .H0(and_6_out), .A1(marge8bit_5_a_out), .B1(marge8bit_5_b_out), .C1(marge8bit_5_c_out),
    .D1(marge8bit_5_d_out), .E1(marge8bit_5_e_out), .F1(marge8bit_5_f_out), .G1(marge8bit_5_g_out),
    .H1(marge8bit_5_h_out), .A_out(marge8bit_6_a_out), .B_out(marge8bit_6_b_out), .C_out(marge8bit_6_c_out),
    .D_out(marge8bit_6_d_out), .E_out(marge8bit_6_e_out), .F_out(marge8bit_6_f_out),
    .G_out(marge8bit_6_g_out), .H_out(marge8bit_6_h_out));
  Marge8bit marge8bit_7 (
    .A0(and_119_out), .B0(and_93_out), .C0(and_94_out), .D0(and_62_out), .E0(and_61_out), .F0(and_29_out),
    .G0(and_30_out), .H0(and_7_out), .A1(marge8bit_6_a_out), .B1(marge8bit_6_b_out), .C1(marge8bit_6_c_out),
    .D1(marge8bit_6_d_out), .E1(marge8bit_6_e_out), .F1(marge8bit_6_f_out), .G1(marge8bit_6_g_out),
    .H1(marge8bit_6_h_out), .A_out(marge8bit_7_a_out), .B_out(marge8bit_7_b_out), .C_out(marge8bit_7_c_out),
    .D_out(marge8bit_7_d_out), .E_out(marge8bit_7_e_out), .F_out(marge8bit_7_f_out),
    .G_out(marge8bit_7_g_out), .H_out(marge8bit_7_h_out));
  and and_119 (and_119_out, _0x06_out, 1'b0);
  and and_120 (and_120_out, _0x07_out, 1'b0);
  Marge8bit marge8bit_8 (
    .A0(and_120_out), .B0(and_96_out), .C0(and_95_out), .D0(and_64_out), .E0(and_63_out), .F0(and_32_out),
    .G0(and_31_out), .H0(and_8_out), .A1(marge8bit_7_a_out), .B1(marge8bit_7_b_out), .C1(marge8bit_7_c_out),
    .D1(marge8bit_7_d_out), .E1(marge8bit_7_e_out), .F1(marge8bit_7_f_out), .G1(marge8bit_7_g_out),
    .H1(marge8bit_7_h_out), .A_out(marge8bit_8_a_out), .B_out(marge8bit_8_b_out), .C_out(marge8bit_8_c_out),
    .D_out(marge8bit_8_d_out), .E_out(marge8bit_8_e_out), .F_out(marge8bit_8_f_out),
    .G_out(marge8bit_8_g_out), .H_out(marge8bit_8_h_out));
  Marge8bit marge8bit_9 (
    .A0(and_121_out), .B0(and_98_out), .C0(and_97_out), .D0(and_65_out), .E0(and_66_out), .F0(and_34_out),
    .G0(and_33_out), .H0(and_9_out), .A1(marge8bit_8_a_out), .B1(marge8bit_8_b_out), .C1(marge8bit_8_c_out),
    .D1(marge8bit_8_d_out), .E1(marge8bit_8_e_out), .F1(marge8bit_8_f_out), .G1(marge8bit_8_g_out),
    .H1(marge8bit_8_h_out), .A_out(marge8bit_9_a_out), .B_out(marge8bit_9_b_out), .C_out(marge8bit_9_c_out),
    .D_out(marge8bit_9_d_out), .E_out(marge8bit_9_e_out), .F_out(marge8bit_9_f_out),
    .G_out(marge8bit_9_g_out), .H_out(marge8bit_9_h_out));
  and and_121 (and_121_out, _0x08_out, 1'b0);
  Marge8bit marge8bit_10 (
    .A0(and_122_out), .B0(and_99_out), .C0(and_100_out), .D0(and_68_out), .E0(and_67_out), .F0(and_36_out),
    .G0(and_35_out), .H0(and_10_out), .A1(marge8bit_9_a_out), .B1(marge8bit_9_b_out), .C1(marge8bit_9_c_out),
    .D1(marge8bit_9_d_out), .E1(marge8bit_9_e_out), .F1(marge8bit_9_f_out), .G1(marge8bit_9_g_out),
    .H1(marge8bit_9_h_out), .A_out(marge8bit_10_a_out), .B_out(marge8bit_10_b_out),
    .C_out(marge8bit_10_c_out), .D_out(marge8bit_10_d_out), .E_out(marge8bit_10_e_out),
    .F_out(marge8bit_10_f_out), .G_out(marge8bit_10_g_out), .H_out(marge8bit_10_h_out));
  and and_122 (and_122_out, _0x09_out, 1'b0);
  and and_123 (and_123_out, _0x0A_out, 1'b0);
  Marge8bit marge8bit_11 (
    .A0(and_123_out), .B0(and_101_out), .C0(and_102_out), .D0(and_70_out), .E0(and_69_out), .F0(and_38_out),
    .G0(and_37_out), .H0(and_11_out), .A1(marge8bit_10_a_out), .B1(marge8bit_10_b_out),
    .C1(marge8bit_10_c_out), .D1(marge8bit_10_d_out), .E1(marge8bit_10_e_out), .F1(marge8bit_10_f_out),
    .G1(marge8bit_10_g_out), .H1(marge8bit_10_h_out), .A_out(marge8bit_11_a_out), .B_out(marge8bit_11_b_out),
    .C_out(marge8bit_11_c_out), .D_out(marge8bit_11_d_out), .E_out(marge8bit_11_e_out),
    .F_out(marge8bit_11_f_out), .G_out(marge8bit_11_g_out), .H_out(marge8bit_11_h_out));
  and and_124 (and_124_out, _0x0B_out, 1'b0);
  Marge8bit marge8bit_12 (
    .A0(and_124_out), .B0(and_103_out), .C0(and_104_out), .D0(and_72_out), .E0(and_71_out), .F0(and_39_out),
    .G0(and_40_out), .H0(and_12_out), .A1(marge8bit_11_a_out), .B1(marge8bit_11_b_out),
    .C1(marge8bit_11_c_out), .D1(marge8bit_11_d_out), .E1(marge8bit_11_e_out), .F1(marge8bit_11_f_out),
    .G1(marge8bit_11_g_out), .H1(marge8bit_11_h_out), .A_out(marge8bit_12_a_out), .B_out(marge8bit_12_b_out),
    .C_out(marge8bit_12_c_out), .D_out(marge8bit_12_d_out), .E_out(marge8bit_12_e_out),
    .F_out(marge8bit_12_f_out), .G_out(marge8bit_12_g_out), .H_out(marge8bit_12_h_out));
  Marge8bit marge8bit_13 (
    .A0(and_125_out), .B0(and_105_out), .C0(and_106_out), .D0(and_74_out), .E0(and_73_out), .F0(and_42_out),
    .G0(and_41_out), .H0(and_13_out), .A1(marge8bit_12_a_out), .B1(marge8bit_12_b_out),
    .C1(marge8bit_12_c_out), .D1(marge8bit_12_d_out), .E1(marge8bit_12_e_out), .F1(marge8bit_12_f_out),
    .G1(marge8bit_12_g_out), .H1(marge8bit_12_h_out), .A_out(marge8bit_13_a_out), .B_out(marge8bit_13_b_out),
    .C_out(marge8bit_13_c_out), .D_out(marge8bit_13_d_out), .E_out(marge8bit_13_e_out),
    .F_out(marge8bit_13_f_out), .G_out(marge8bit_13_g_out), .H_out(marge8bit_13_h_out));
  and and_125 (and_125_out, _0x0C_out, 1'b0);
  Marge8bit marge8bit_14 (
    .A0(and_126_out), .B0(and_108_out), .C0(and_107_out), .D0(and_75_out), .E0(and_76_out), .F0(and_44_out),
    .G0(and_43_out), .H0(and_14_out), .A1(marge8bit_13_a_out), .B1(marge8bit_13_b_out),
    .C1(marge8bit_13_c_out), .D1(marge8bit_13_d_out), .E1(marge8bit_13_e_out), .F1(marge8bit_13_f_out),
    .G1(marge8bit_13_g_out), .H1(marge8bit_13_h_out), .A_out(marge8bit_14_a_out), .B_out(marge8bit_14_b_out),
    .C_out(marge8bit_14_c_out), .D_out(marge8bit_14_d_out), .E_out(marge8bit_14_e_out),
    .F_out(marge8bit_14_f_out), .G_out(marge8bit_14_g_out), .H_out(marge8bit_14_h_out));
  and and_126 (and_126_out, _0x0D_out, 1'b0);
  and and_127 (and_127_out, _0x0E_out, 1'b0);
  Marge8bit marge8bit_15 (
    .A0(and_127_out), .B0(and_109_out), .C0(and_110_out), .D0(and_78_out), .E0(and_77_out), .F0(and_46_out),
    .G0(and_45_out), .H0(and_15_out), .A1(marge8bit_14_a_out), .B1(marge8bit_14_b_out),
    .C1(marge8bit_14_c_out), .D1(marge8bit_14_d_out), .E1(marge8bit_14_e_out), .F1(marge8bit_14_f_out),
    .G1(marge8bit_14_g_out), .H1(marge8bit_14_h_out), .A_out(marge8bit_15_a_out), .B_out(marge8bit_15_b_out),
    .C_out(marge8bit_15_c_out), .D_out(marge8bit_15_d_out), .E_out(marge8bit_15_e_out),
    .F_out(marge8bit_15_f_out), .G_out(marge8bit_15_g_out), .H_out(marge8bit_15_h_out));
  and and_128 (and_128_out, _0x0F_out, 1'b0);
  Marge8bit marge8bit_16 (
    .A0(and_128_out), .B0(and_112_out), .C0(and_111_out), .D0(and_79_out), .E0(and_80_out), .F0(and_48_out),
    .G0(and_47_out), .H0(and_16_out), .A1(marge8bit_15_a_out), .B1(marge8bit_15_b_out),
    .C1(marge8bit_15_c_out), .D1(marge8bit_15_d_out), .E1(marge8bit_15_e_out), .F1(marge8bit_15_f_out),
    .G1(marge8bit_15_g_out), .H1(marge8bit_15_h_out), .A_out(bit0), .B_out(bit1), .C_out(bit2), .D_out(bit3),
    .E_out(bit4), .F_out(bit5), .G_out(bit6), .H_out(bit7));

  // Notes on the sheet:
  //   0000 add a,im
  //   0001 mov a,b
  //   0010 in a
  //   0011 mov a,im
  //   0100 mov b,a
  //   0101 add b,a
  //   0110 mov b,im
  //   0111 mov b,im
  //   1001 out b
  //   1011 out im
  //   1110 jnc
  //   1111 jmp
endmodule

// SLCT16
module Selector16bit (
  input  SELECT_A,
  input  SELECT_B,
  input  SELECT_C,
  input  SELECT_D,
  input  C0_in,
  input  C1_in,
  input  C2_in,
  input  C3_in,
  input  C4_in,
  input  C5_in,
  input  C6_in,
  input  C7_in,
  input  C8_in,
  input  C9_in,
  input  C10_in,
  input  C11_in,
  input  C12_in,
  input  C13_in,
  input  C14_in,
  input  C15_in,
  output out_21
);

  wire and_1_out, and_2_out, not_1_out, selecter8bit_1_out_12, selecter8bit_2_out_12;

  Selecter8bit selecter8bit_1 (
    .SELECT_A(SELECT_A), .SELECT_B(SELECT_B), .SELECT_C(SELECT_C), .C0_in(C0_in), .C1_in(C1_in),
    .C2_in(C2_in), .C3_in(C3_in), .C4_in(C4_in), .C5_in(C5_in), .C6_in(C6_in), .C7_in(C7_in),
    .out_12(selecter8bit_1_out_12));
  Selecter8bit selecter8bit_2 (
    .SELECT_A(SELECT_A), .SELECT_B(SELECT_B), .SELECT_C(SELECT_C), .C0_in(C8_in), .C1_in(C9_in),
    .C2_in(C10_in), .C3_in(C11_in), .C4_in(C12_in), .C5_in(C13_in), .C6_in(C14_in), .C7_in(C15_in),
    .out_12(selecter8bit_2_out_12));
  not not_1 (not_1_out, SELECT_D);
  and and_1 (and_1_out, selecter8bit_1_out_12, not_1_out);
  and and_2 (and_2_out, selecter8bit_2_out_12, SELECT_D);
  or or_1 (out_21, and_1_out, and_2_out);
endmodule

// AND
module AND2 (
  input  A_in,
  input  B_in,
  output C_out
);

  and and_1 (C_out, A_in, B_in);

  // Notes on the sheet:
  //   ちっちゃいやつが欲しかった
endmodule

module Marge8bit (
  input  A1,
  input  B1,
  input  C1,
  input  D1,
  input  E1,
  input  F1,
  input  G1,
  input  H1,
  input  A0,
  input  B0,
  input  C0,
  input  D0,
  input  E0,
  input  F0,
  input  G0,
  input  H0,
  output A_out,
  output B_out,
  output C_out,
  output D_out,
  output E_out,
  output F_out,
  output G_out,
  output H_out
);

  or or_1 (A_out, A1, A0);
  or or_2 (B_out, B1, B0);
  or or_3 (C_out, C1, C0);
  or or_4 (D_out, D1, D0);
  or or_5 (E_out, E1, E0);
  or or_6 (F_out, F1, F0);
  or or_7 (G_out, G1, G0);
  or or_8 (H_out, H1, H0);
endmodule

// RGST_TD4
module Registories (
  input  RST__When_1__clear_register,
  input  CLK,
  input  LoadA__When_0_load_input,
  input  LoadB__When_0_load_input,
  input  LoadC__When_0_load_input,
  input  LoadD__When_0_load_input,
  input  A_in,
  input  B_in,
  input  C_in,
  input  D_in,
  input  SELECT_A,
  input  SELECT_B,
  input  SW_0,
  input  SW_1,
  input  SW_2,
  input  SW_3,
  output LED0,
  output LED1,
  output PRG_0,
  output LED2,
  output PRG_1,
  output LED3,
  output PRG_2,
  output PRG_3,
  output A_out,
  output B_out,
  output C_out,
  output D_out
);

  wire A_qa_out, A_qb_out, A_qc_out, A_qd_out, B_qa_out, B_qb_out, B_qc_out, B_qd_out;

  Register4bit A (
    .RST__When_1__outputs_are_0(RST__When_1__clear_register), .CLK(CLK),
    .LD__When_0_load_input(LoadA__When_0_load_input), .A_in(A_in), .B_in(B_in), .C_in(C_in), .D_in(D_in),
    .QA_out(A_qa_out), .QB_out(A_qb_out), .QC_out(A_qc_out), .QD_out(A_qd_out));
  Register4bit B (
    .RST__When_1__outputs_are_0(RST__When_1__clear_register), .CLK(CLK),
    .LD__When_0_load_input(LoadB__When_0_load_input), .A_in(A_in), .B_in(B_in), .C_in(C_in), .D_in(D_in),
    .QA_out(B_qa_out), .QB_out(B_qb_out), .QC_out(B_qc_out), .QD_out(B_qd_out));
  Register4bit C (
    .RST__When_1__outputs_are_0(RST__When_1__clear_register), .CLK(CLK),
    .LD__When_0_load_input(LoadC__When_0_load_input), .A_in(A_in), .B_in(B_in), .C_in(C_in), .D_in(D_in),
    .QA_out(LED0), .QB_out(LED1), .QC_out(LED2), .QD_out(LED3));
  ProgramCounter D (
    .RST__When_1__outputs_are_0(RST__When_1__clear_register), .CLK(CLK),
    .LD__When_0_load_input(LoadD__When_0_load_input), .A_in(A_in), .B_in(B_in), .C_in(C_in), .D_in(D_in),
    .QA_out(PRG_0), .QB_out(PRG_1), .QC_out(PRG_2), .QD_out(PRG_3));
  Selecter4bit selecter4bit_1 (
    .SELECT_A(SELECT_A), .SELECT_B(SELECT_B), .C0_in(A_qa_out), .C1_in(B_qa_out), .C2_in(SW_0), .C3_in(1'b0),
    .C_out(A_out));
  Selecter4bit selecter4bit_2 (
    .SELECT_A(SELECT_A), .SELECT_B(SELECT_B), .C0_in(A_qb_out), .C1_in(B_qb_out), .C2_in(SW_1), .C3_in(1'b0),
    .C_out(B_out));
  Selecter4bit selecter4bit_3 (
    .SELECT_A(SELECT_A), .SELECT_B(SELECT_B), .C0_in(A_qc_out), .C1_in(B_qc_out), .C2_in(SW_2), .C3_in(1'b0),
    .C_out(C_out));
  Selecter4bit selecter4bit_4 (
    .SELECT_A(SELECT_A), .SELECT_B(SELECT_B), .C0_in(A_qd_out), .C1_in(B_qd_out), .C2_in(SW_3), .C3_in(1'b0),
    .C_out(D_out));
endmodule

// DCD_TD4
module Decoder_TD4 (
  input  bit7,
  input  bit6,
  input  bit5,
  input  bit4,
  input  C_flag,
  output LOAD_A,
  output LOAD_B,
  output LOAD_C,
  output LOAD_D,
  output SELECT_A,
  output SELECT_B
);

  wire and_1_out, not_1_out, not_2_out, not_3_out, not_4_out, not_5_out;

  not not_1 (not_1_out, bit6);
  not not_2 (not_2_out, bit7);
  not not_3 (not_3_out, bit6);
  not not_4 (not_4_out, bit7);
  not not_5 (not_5_out, bit4);
  and and_1 (and_1_out, not_5_out, C_flag);
  or or_1 (LOAD_A, bit7, bit6);
  or or_2 (LOAD_B, not_1_out, bit7);
  or or_3 (LOAD_C, not_2_out, bit6);
  or or_4 (LOAD_D, not_3_out, not_4_out, and_1_out);
  or or_5 (SELECT_A, bit4, bit7);

  assign SELECT_B = bit5;

  // Notes on the sheet:
  //   op3,2,1,0,flag
endmodule

// PG_CNT
module ProgramCounter (
  input  RST__When_1__outputs_are_0,
  input  CLK,
  input  LD__When_0_load_input,
  input  A_in,
  input  B_in,
  input  C_in,
  input  D_in,
  output QA_out,
  output QB_out,
  output QC_out,
  output QD_out
);

  wire and_1_out, and_2_out, and_3_out, and_4_out, and_5_out, and_6_out, and_7_out, and_8_out,
       fulladder4bit_1_s0_out, fulladder4bit_1_s1_out, fulladder4bit_1_s2_out, fulladder4bit_1_s3_out,
       not_1_out, or_1_out, or_2_out, or_3_out, or_4_out;

  not not_1 (not_1_out, LD__When_0_load_input);
  and and_1 (and_1_out, not_1_out, A_in);
  and and_2 (and_2_out, not_1_out, B_in);
  and and_3 (and_3_out, not_1_out, C_in);
  and and_4 (and_4_out, not_1_out, D_in);
  or or_1 (or_1_out, and_1_out, and_5_out);
  or or_2 (or_2_out, and_2_out, and_6_out);
  or or_3 (or_3_out, and_3_out, and_7_out);
  or or_4 (or_4_out, and_4_out, and_8_out);
  Register4bit register4bit_1 (
    .RST__When_1__outputs_are_0(RST__When_1__outputs_are_0), .CLK(CLK), .LD__When_0_load_input(1'b0),
    .A_in(or_1_out), .B_in(or_2_out), .C_in(or_3_out), .D_in(or_4_out), .QA_out(QA_out), .QB_out(QB_out),
    .QC_out(QC_out), .QD_out(QD_out));
  FullAdder4bit fulladder4bit_1 (
    .Carry_in(1'b1), .A0_in(1'b0), .B0_in(QA_out), .A1_in(1'b0), .B1_in(QB_out), .A2_in(1'b0),
    .B2_in(QC_out), .A3_in(1'b0), .B3_in(QD_out), .S0_out(fulladder4bit_1_s0_out),
    .S1_out(fulladder4bit_1_s1_out), .S2_out(fulladder4bit_1_s2_out), .S3_out(fulladder4bit_1_s3_out));  // open: C_out__Carry_out
  and and_5 (and_5_out, LD__When_0_load_input, fulladder4bit_1_s0_out);
  and and_6 (and_6_out, LD__When_0_load_input, fulladder4bit_1_s1_out);
  and and_7 (and_7_out, LD__When_0_load_input, fulladder4bit_1_s2_out);
  and and_8 (and_8_out, LD__When_0_load_input, fulladder4bit_1_s3_out);

  // Notes on the sheet:
  //   Loadが0ならロードして，1なら加算
  //   タイマーなし74HC161みたいなやつ(P185)
endmodule
