// Logisim project TM8.circ as structural Verilog: 11 circuits, main circuit main
module main (
  input  [7:0] \input ,
  output [7:0] im_data,
  output [7:0] data_a,
  output [7:0] cmd,
  output [7:0] data_b,
  output [2:0] load,
  output [2:0] cmp,
  output [2:0] sa,
  output [2:0] sb,
  output [2:0] op,
  output [7:0] data,
  output [7:0] in,
  output [7:0] pgm_cnt
);

  wire button_1_out, clock_1_out, decoder_1_store_ram__1_if_store_ram, decoder_1_use_im__1_if_use_imdata,
       decoder_1_use_ram__1_if_read_ram, or_1_out;
  wire [7:0] alu_1_result, ram_1_data, register_1_b_out, register_1_led_out;

  Decoder decoder_1 (
    .cmp(cmp), .cmd(cmd), .loads(load), .select_a(sa), .select_b(sb), .operation(op),
    .use_im__1_if_use_imdata(decoder_1_use_im__1_if_use_imdata),
    .store_ram__1_if_store_ram(decoder_1_store_ram__1_if_store_ram),
    .use_ram__1_if_read_ram(decoder_1_use_ram__1_if_read_ram));
  Clock clock_1 (.out(clock_1_out));
  Button button_1 (.out(button_1_out));
  Selector_2 selector_2_1 (
    .use_a__1_if_use_a(decoder_1_use_im__1_if_use_imdata), .a_in(im_data), .b_in(\input ), .out_4(in));
  Register register_1 (
    .load(load), .clock(clock_1_out), .clear(button_1_out), .data(data), .select_a(sa), .select_b(sb),
    .\input (in), .a_out(data_a), .b_out(register_1_b_out), .cmp(cmp), .led_out(register_1_led_out),
    .pgm_cnt(pgm_cnt));
  Selector_2 selector_2_2 (
    .use_a__1_if_use_a(decoder_1_store_ram__1_if_store_ram), .a_in({8{1'b0}}), .b_in(register_1_b_out),
    .out_4(data_b));
  or or_1 (or_1_out, decoder_1_store_ram__1_if_store_ram, decoder_1_use_ram__1_if_read_ram);
  ROM #(.dataWidth(16)) rom_1 (.addr(pgm_cnt), .data({cmd, im_data}));  // open: sel
  ALU alu_1 (.data_a(data_a), .data_b(data_b), .operation(op), .result(alu_1_result));
  RAM #(.bus("separate")) ram_1 (
    .addr(data_a), .din(register_1_b_out), .data(ram_1_data), .str(decoder_1_store_ram__1_if_store_ram),
    .sel(or_1_out), .clk(clock_1_out), .clr(button_1_out));  // open: ld
  Selector_2 selector_2_3 (
    .use_a__1_if_use_a(decoder_1_use_ram__1_if_read_ram), .a_in(ram_1_data), .b_in(alu_1_result), .out_4(data));
  LED led_1 (.in(register_1_led_out[0]));
  LED led_2 (.in(register_1_led_out[1]));
  LED led_3 (.in(register_1_led_out[2]));
  LED led_4 (.in(register_1_led_out[3]));
  LED led_5 (.in(register_1_led_out[4]));
  LED led_6 (.in(register_1_led_out[5]));
  LED led_7 (.in(register_1_led_out[6]));
  LED led_8 (.in(register_1_led_out[7]));

  // Notes on the sheet:
  //   contents of rom_1 (hex, n*v repeats v):
  //   0 4700 4f00 5700 5f00 6700 5f01 9700 0 0 0 5f01 0 0 5700 0 0 6200 9000 4b00 8200 9400 0 1001 140a
  //   cf1b 7f0f 0 0 0 5700 0 0 6200 9000 40a d746 0 0 4800 b0a 0 0 6714 9500 0 0 a0a 0 0 8100 0 0 6200
  //   9400 0 0 0 6714 9100 0 1001 6200 1101 0 0 9000 8000 9400 0 0 1001 140a cf4b 7f1f 0 0 0 1801 1c0a
  //   cf52 7f0c 0 0 77ff 7700 7f52
endmodule

module ALU (
  input  [7:0] data_a,
  input  [7:0] data_b,
  input  [2:0] operation,
  output [7:0] result
);

  wire decoder_1_out0, decoder_1_out1, decoder_1_out2, decoder_1_out3, decoder_1_out4, decoder_1_out5,
       decoder_1_out6, decoder_1_out7;
  wire [2:0] comparator_1_gt;
  wire [7:0] adder_1_out, and_1_out, bit_extender_1_out, divider_1_out, multiplier_1_out, not_1_out,
       or_1_out, subtractor_1_out;

  Adder adder_1 (.a(data_a), .b(data_b), .out(adder_1_out), .cin(1'b0));  // open: cout
  Subtractor subtractor_1 (.a(data_a), .b(data_b), .out(subtractor_1_out), .bin(1'b0));  // open: bout
  Multiplier multiplier_1 (.a(data_a), .b(data_b), .out(multiplier_1_out));  // open: cin, cout
  Divider divider_1 (.a(data_a), .b(data_b), .out(divider_1_out));  // open: upper, rem
  Comparator comparator_1 (
    .a(data_a), .b(data_b), .gt(comparator_1_gt[0]), .eq(comparator_1_gt[1]), .lt(comparator_1_gt[2]));
  assign and_1_out = data_a & data_b;  // AND_Gate and_1, 8 bits wide
  assign or_1_out = data_a | data_b;  // OR_Gate or_1, 8 bits wide
  assign not_1_out = ~data_a;  // NOT_Gate not_1, 8 bits wide
  assign bit_extender_1_out = {{5{1'b0}}, comparator_1_gt};  // Bit_Extender bit_extender_1
  Decoder_part #(.select(3)) decoder_1 (
    .out0(decoder_1_out0), .out1(decoder_1_out1), .out2(decoder_1_out2), .out3(decoder_1_out3),
    .out4(decoder_1_out4), .out5(decoder_1_out5), .out6(decoder_1_out6), .out7(decoder_1_out7),
    .sel(operation));  // open: en
  assign result = decoder_1_out0 ? adder_1_out : 8'bz;  // Controlled_Buffer controlled_buffer_1
  assign result = decoder_1_out1 ? subtractor_1_out : 8'bz;  // Controlled_Buffer controlled_buffer_2
  assign result = decoder_1_out2 ? multiplier_1_out : 8'bz;  // Controlled_Buffer controlled_buffer_3
  assign result = decoder_1_out3 ? divider_1_out : 8'bz;  // Controlled_Buffer controlled_buffer_4
  assign result = decoder_1_out4 ? bit_extender_1_out : 8'bz;  // Controlled_Buffer controlled_buffer_5
  assign result = decoder_1_out5 ? and_1_out : 8'bz;  // Controlled_Buffer controlled_buffer_6
  assign result = decoder_1_out6 ? or_1_out : 8'bz;  // Controlled_Buffer controlled_buffer_7
  assign result = decoder_1_out7 ? not_1_out : 8'bz;  // Controlled_Buffer controlled_buffer_8

  // Notes on the sheet:
  //   a?b
endmodule

// DECD
module Decoder (
  input  [2:0] cmp,
  input  [7:0] cmd,
  output [2:0] loads,
  output [2:0] select_a,
  output [2:0] select_b,
  output [2:0] operation,
  output use_im__1_if_use_imdata,
  output store_ram__1_if_store_ram,
  output use_ram__1_if_read_ram
);

  wire and_1_out, and_2_out, and_3_out, and_4_out, and_5_out, and_6_out, and_7_out, and_8_out, not_1_out,
       not_2_out, not_3_out, not_4_out, not_5_out, not_6_out, not_7_out, not_8_out, not_9_out, not_10_out,
       not_11_out, not_12_out, not_13_out, not_14_out, not_15_out, not_16_out, not_17_out, or_1_out;
  wire [2:0] load_decoder_1__out03, select_a_decoder_1__out2, selector_2_3bit_1_out_4,
       selector_2_3bit_3_out_4;

  Load_decoder load_decoder_1 (
    ._in0(cmd[7]), ._in1(cmd[6]), ._in2(cmd[5]), ._in3(cmd[4]), ._in4(cmd[3]), ._in5(cmd[2]), ._in6(cmd[1]),
    ._in7(cmd[0]), ._out0(load_decoder_1__out03[2]), ._out02(load_decoder_1__out03[1]),
    ._out03(load_decoder_1__out03[0]));
  not not_1 (not_1_out, cmd[5]);
  not not_2 (not_2_out, cmd[3]);
  not not_3 (not_3_out, cmd[4]);
  not not_4 (not_4_out, cmd[5]);
  not not_5 (not_5_out, cmd[4]);
  not not_6 (not_6_out, cmd[5]);
  not not_7 (not_7_out, cmd[3]);
  not not_8 (not_8_out, cmd[5]);
  Select_a_decoder select_a_decoder_1 (
    ._in0(cmd[7]), ._in1(cmd[6]), ._in2(cmd[5]), ._in3(cmd[4]), ._in4(cmd[3]), ._in5(cmd[2]), ._in6(cmd[1]),
    ._in7(cmd[0]), ._out0(select_a_decoder_1__out2[2]), ._out1(select_a_decoder_1__out2[1]),
    ._out2(select_a_decoder_1__out2[0]));
  Select_b_decoder select_b_decoder_1 (
    ._in0(cmd[7]), ._in1(cmd[6]), ._in2(cmd[5]), ._in3(cmd[4]), ._in4(cmd[3]), ._in5(cmd[2]), ._in6(cmd[1]),
    ._in7(cmd[0]), ._out0(select_b[2]), ._out02(select_b[1]), ._out03(select_b[0]));
  Operation_decoder operation_decoder_1 (
    ._in0(cmd[7]), ._in1(cmd[6]), ._in2(cmd[5]), ._in3(cmd[4]), ._in4(cmd[3]), ._in5(cmd[2]), ._in6(cmd[1]),
    ._in7(cmd[0]), ._out0(operation[2]), ._out1(operation[1]), ._out2(operation[0]));
  not not_9 (not_9_out, cmd[7]);
  not not_10 (not_10_out, cmd[5]);
  not not_11 (not_11_out, cmd[3]);
  not not_12 (not_12_out, cmd[5]);
  not not_13 (not_13_out, cmd[6]);
  not not_14 (not_14_out, cmd[2]);
  not not_15 (not_15_out, cmd[3]);
  not not_16 (not_16_out, cmd[5]);
  not not_17 (not_17_out, cmd[6]);
  and and_1 (and_1_out, not_1_out, cmd[6], cmd[7]);
  and and_2 (and_2_out, cmp[0], and_3_out);
  and and_3 (and_3_out, not_2_out, not_3_out, not_4_out, cmd[6], cmd[7]);
  and and_4 (and_4_out, cmp[1], and_5_out);
  and and_5 (and_5_out, cmd[3], not_5_out, not_6_out, cmd[6], cmd[7]);
  and and_6 (and_6_out, cmp[2], and_7_out);
  and and_7 (and_7_out, not_7_out, cmd[4], not_8_out, cmd[6], cmd[7]);
  and and_8 (and_8_out, not_10_out, cmd[6], cmd[7]);
  or or_1 (or_1_out, and_2_out, and_4_out, and_6_out);
  or or_2 (use_im__1_if_use_imdata, not_9_out, and_8_out);
  and and_9 (store_ram__1_if_store_ram, cmd[2], not_11_out, cmd[4], not_12_out, not_13_out, cmd[7]);
  and and_10 (use_ram__1_if_read_ram, not_14_out, not_15_out, cmd[4], not_16_out, not_17_out, cmd[7]);
  Selector_2_3bit selector_2_3bit_1 (
    .use_a__1_if_use_a(or_1_out), .a_in(3'b111), .b_in(3'b000), .out_4(selector_2_3bit_1_out_4));
  Selector_2_3bit selector_2_3bit_2 (
    .use_a__1_if_use_a(and_1_out), .a_in(selector_2_3bit_1_out_4), .b_in(load_decoder_1__out03), .out_4(loads));
  Selector_2_3bit selector_2_3bit_3 (
    .use_a__1_if_use_a(or_1_out), .a_in(cmd[2:0]), .b_in(3'b000), .out_4(selector_2_3bit_3_out_4));
  Selector_2_3bit selector_2_3bit_4 (
    .use_a__1_if_use_a(and_1_out), .a_in(selector_2_3bit_3_out_4), .b_in(select_a_decoder_1__out2),
    .out_4(select_a));

  // Notes on the sheet:
  //   a,b,c,d...を出力
  //   下のほうならTrue
  //   うみゃーっ！！！
  //   flagがTrueならTrue
endmodule

// REG
module Register (
  input  [2:0] load,
  input  clock,
  input  clear,
  input  [7:0] data,
  input  [2:0] select_a,
  input  [2:0] select_b,
  input  [7:0] \input ,
  output [7:0] a_out,
  output [7:0] b_out,
  output [2:0] cmp,
  output [7:0] led_out,
  output [7:0] pgm_cnt
);

  wire decoder_1_out0, decoder_1_out1, decoder_1_out2, decoder_1_out3, decoder_1_out4, decoder_1_out5,
       decoder_1_out6, decoder_1_out7;
  wire [7:0] A_q, adder_1_out, B_q, C_q, D_q, E_q, selector_2_1_out_4;
  wire [7:3] F_cmp_q;

  Decoder_part #(.select(3)) decoder_1 (
    .out0(decoder_1_out0), .out1(decoder_1_out1), .out2(decoder_1_out2), .out3(decoder_1_out3),
    .out4(decoder_1_out4), .out5(decoder_1_out5), .out6(decoder_1_out6), .out7(decoder_1_out7), .sel(load));  // open: en
  Register_part A (.D(data), .en(decoder_1_out0), .Q(A_q), .clk(clock), .clr(clear));
  Register_part B (.D(data), .en(decoder_1_out1), .Q(B_q), .clk(clock), .clr(clear));
  Register_part C (.D(data), .en(decoder_1_out2), .Q(C_q), .clk(clock), .clr(clear));
  Register_part D (.D(data), .en(decoder_1_out3), .Q(D_q), .clk(clock), .clr(clear));
  Register_part E (.D(data), .en(decoder_1_out4), .Q(E_q), .clk(clock), .clr(clear));
  Register_part F_cmp (.D(data), .en(decoder_1_out5), .Q({F_cmp_q, cmp}), .clk(clock), .clr(clear));
  Register_part G_out (.D(data), .en(decoder_1_out6), .Q(led_out), .clk(clock), .clr(clear));
  Selector_2 selector_2_1 (
    .use_a__1_if_use_a(decoder_1_out7), .a_in(data), .b_in(adder_1_out), .out_4(selector_2_1_out_4));
  Register_part H_cnt (.D(selector_2_1_out_4), .en(1'b1), .Q(pgm_cnt), .clk(clock), .clr(clear));
  Adder adder_1 (.a(pgm_cnt), .b(8'h1), .out(adder_1_out));  // open: cin, cout
  Selector_8 selector_8_1 (
    .select(select_a), .data_0(A_q), .data_1(B_q), .data_2(C_q), .data_3(D_q), .data_4(E_q),
    .data_5(pgm_cnt), .data_6({8{1'b0}}), .data_7(\input ), .out_10(a_out));
  Selector_8 selector_8_2 (
    .select(select_b), .data_0(A_q), .data_1(B_q), .data_2(C_q), .data_3(D_q), .data_4(E_q),
    .data_5(pgm_cnt), .data_6({8{1'b0}}), .data_7(\input ), .out_10(b_out));
endmodule

module Selector_8 (
  input  [2:0] select,
  input  [7:0] data_0,
  input  [7:0] data_1,
  input  [7:0] data_2,
  input  [7:0] data_3,
  input  [7:0] data_4,
  input  [7:0] data_5,
  input  [7:0] data_6,
  input  [7:0] data_7,
  output [7:0] out_10
);

  wire decoder_1_out0, decoder_1_out1, decoder_1_out2, decoder_1_out3, decoder_1_out4, decoder_1_out5,
       decoder_1_out6, decoder_1_out7;

  Decoder_part #(.select(3)) decoder_1 (
    .out0(decoder_1_out0), .out1(decoder_1_out1), .out2(decoder_1_out2), .out3(decoder_1_out3),
    .out4(decoder_1_out4), .out5(decoder_1_out5), .out6(decoder_1_out6), .out7(decoder_1_out7), .sel(select));  // open: en
  assign out_10 = decoder_1_out0 ? data_0 : 8'bz;  // Controlled_Buffer controlled_buffer_1
  assign out_10 = decoder_1_out1 ? data_1 : 8'bz;  // Controlled_Buffer controlled_buffer_2
  assign out_10 = decoder_1_out2 ? data_2 : 8'bz;  // Controlled_Buffer controlled_buffer_3
  assign out_10 = decoder_1_out3 ? data_3 : 8'bz;  // Controlled_Buffer controlled_buffer_4
  assign out_10 = decoder_1_out4 ? data_4 : 8'bz;  // Controlled_Buffer controlled_buffer_5
  assign out_10 = decoder_1_out5 ? data_5 : 8'bz;  // Controlled_Buffer controlled_buffer_6
  assign out_10 = decoder_1_out6 ? data_6 : 8'bz;  // Controlled_Buffer controlled_buffer_7
  assign out_10 = decoder_1_out7 ? data_7 : 8'bz;  // Controlled_Buffer controlled_buffer_8
endmodule

// SLCT
module Selector_2 (
  input  use_a__1_if_use_a,
  input  [7:0] a_in,
  input  [7:0] b_in,
  output [7:0] out_4
);

  wire not_1_out;

  not not_1 (not_1_out, use_a__1_if_use_a);
  assign out_4 = use_a__1_if_use_a ? a_in : 8'bz;  // Controlled_Buffer controlled_buffer_1
  assign out_4 = not_1_out ? b_in : 8'bz;  // Controlled_Buffer controlled_buffer_2
endmodule

module Operation_decoder (
  input  _in0,
  input  _in1,
  input  _in2,
  input  _in3,
  input  _in4,
  input  _in5,
  input  _in6,
  input  _in7,
  output _out0,
  output _out1,
  output _out2
);

  wire and_1_out, and_2_out, and_3_out, and_4_out, and_5_out, and_6_out, and_7_out, and_8_out, and_9_out,
       and_10_out, and_11_out, and_12_out, and_13_out, not_1_out, not_2_out, not_3_out, not_4_out, not_5_out,
       not_6_out, not_7_out, not_8_out, not_9_out, not_10_out, not_11_out, not_12_out, not_13_out,
       not_14_out, not_15_out, not_16_out;

  not not_1 (not_1_out, _in0);
  not not_2 (not_2_out, _in1);
  not not_3 (not_3_out, _in1);
  not not_4 (not_4_out, _in3);
  not not_5 (not_5_out, _in6);
  not not_6 (not_6_out, _in1);
  not not_7 (not_7_out, _in3);
  not not_8 (not_8_out, _in7);
  not not_9 (not_9_out, _in0);
  not not_10 (not_10_out, _in1);
  and and_1 (and_1_out, not_9_out, not_10_out, _in6);
  not not_11 (not_11_out, _in1);
  not not_12 (not_12_out, _in3);
  and and_2 (and_2_out, not_11_out, not_12_out, _in6);
  and and_3 (and_3_out, _in0, _in2);
  and and_4 (and_4_out, _in0, _in1, _in3, _in4);
  not not_13 (not_13_out, _in0);
  and and_5 (and_5_out, not_13_out, not_14_out, _in7);
  not not_14 (not_14_out, _in1);
  not not_15 (not_15_out, _in1);
  and and_6 (and_6_out, not_15_out, not_16_out, _in7);
  not not_16 (not_16_out, _in3);
  and and_7 (and_7_out, _in0, _in2);
  and and_8 (and_8_out, _in0, _in1, _in3, _in4);
  and and_9 (and_9_out, not_1_out, not_2_out, _in5);
  and and_10 (and_10_out, not_3_out, not_4_out, _in5, not_5_out);
  and and_11 (and_11_out, not_6_out, not_7_out, _in5, not_8_out);
  and and_12 (and_12_out, _in0, _in2);
  and and_13 (and_13_out, _in0, _in1, _in3, _in4);
  or or_1 (_out1, and_1_out, and_2_out, and_3_out, and_4_out);
  or or_2 (_out2, and_5_out, and_6_out, and_7_out, and_8_out);
  or or_3 (_out0, and_9_out, and_10_out, and_11_out, and_12_out, and_13_out);
endmodule

module Select_a_decoder (
  input  _in0,
  input  _in1,
  input  _in2,
  input  _in3,
  input  _in4,
  input  _in5,
  input  _in6,
  input  _in7,
  output _out0,
  output _out1,
  output _out2
);

  wire and_1_out, and_2_out, and_3_out, and_4_out, and_5_out, and_6_out, and_7_out, and_8_out, and_9_out,
       and_10_out, and_11_out, and_12_out, and_13_out, and_14_out, and_15_out, and_16_out, and_17_out,
       and_18_out, and_19_out, and_20_out, and_21_out, and_22_out, and_23_out, and_24_out, not_1_out,
       not_2_out, not_3_out, not_4_out, not_5_out, not_6_out, not_7_out, not_8_out, not_9_out, not_10_out,
       not_11_out, not_12_out, not_13_out, not_14_out, not_15_out, not_16_out, not_17_out, not_18_out,
       not_19_out, not_20_out, not_21_out, not_22_out, not_23_out, not_24_out, not_25_out, not_26_out,
       not_27_out;

  not not_1 (not_1_out, _in1);
  not not_2 (not_2_out, _in3);
  not not_3 (not_3_out, _in0);
  not not_4 (not_4_out, _in1);
  not not_5 (not_5_out, _in4);
  not not_6 (not_6_out, _in1);
  not not_7 (not_7_out, _in5);
  not not_8 (not_8_out, _in0);
  not not_9 (not_9_out, _in1);
  not not_10 (not_10_out, _in0);
  not not_11 (not_11_out, _in0);
  not not_12 (not_12_out, _in4);
  not not_13 (not_13_out, _in5);
  not not_14 (not_14_out, _in2);
  not not_15 (not_15_out, _in5);
  not not_16 (not_16_out, _in0);
  not not_17 (not_17_out, _in4);
  not not_18 (not_18_out, _in2);
  not not_19 (not_19_out, _in0);
  not not_20 (not_20_out, _in1);
  not not_21 (not_21_out, _in1);
  not not_22 (not_22_out, _in3);
  not not_23 (not_23_out, _in1);
  not not_24 (not_24_out, _in3);
  not not_25 (not_25_out, _in0);
  not not_26 (not_26_out, _in5);
  not not_27 (not_27_out, _in0);
  and and_1 (and_1_out, not_1_out, _in2);
  and and_2 (and_2_out, _in2, _in5);
  and and_3 (and_3_out, _in2, not_2_out, _in4);
  and and_4 (and_4_out, not_3_out, _in1, _in5, _in6, _in7);
  and and_5 (and_5_out, _in0, not_4_out, _in3, not_5_out);
  and and_6 (and_6_out, _in0, not_6_out, _in3, not_7_out);
  and and_7 (and_7_out, _in0, _in2);
  and and_8 (and_8_out, not_8_out, not_9_out, _in3);
  and and_9 (and_9_out, not_10_out, _in3, _in6);
  and and_10 (and_10_out, not_11_out, _in1, not_12_out, not_13_out, _in6);
  and and_11 (and_11_out, _in1, not_14_out, not_15_out, _in6);
  and and_12 (and_12_out, not_16_out, _in1, not_17_out, _in6, _in7);
  and and_13 (and_13_out, _in1, not_18_out, _in6, _in7);
  and and_14 (and_14_out, _in1, _in3, _in5);
  and and_15 (and_15_out, _in0, _in3, _in4);
  and and_16 (and_16_out, _in0, _in2, _in3);
  and and_17 (and_17_out, not_19_out, not_20_out, _in4);
  and and_18 (and_18_out, not_21_out, not_22_out, _in4);
  and and_19 (and_19_out, _in4, _in5);
  and and_20 (and_20_out, not_23_out, _in2, _in4);
  and and_21 (and_21_out, _in2, not_24_out, _in4);
  and and_22 (and_22_out, not_25_out, _in1, not_26_out, _in7);
  and and_23 (and_23_out, not_27_out, _in1, _in6, _in7);
  and and_24 (and_24_out, _in0, _in1, _in4);
  or or_1 (_out0, and_1_out, and_2_out, and_3_out, and_4_out, and_5_out, and_6_out, and_7_out);
  or or_2 (_out1, and_8_out, and_9_out, and_10_out, and_11_out, and_12_out, and_13_out, and_14_out, and_15_out, and_16_out);
  or or_3 (_out2, and_17_out, and_18_out, and_19_out, and_20_out, and_21_out, and_22_out, and_23_out, and_24_out);
endmodule

module Selector_2_3bit (
  input  use_a__1_if_use_a,
  input  [2:0] a_in,
  input  [2:0] b_in,
  output [2:0] out_4
);

  wire not_1_out;

  not not_1 (not_1_out, use_a__1_if_use_a);
  assign out_4 = use_a__1_if_use_a ? a_in : 3'bz;  // Controlled_Buffer controlled_buffer_1
  assign out_4 = not_1_out ? b_in : 3'bz;  // Controlled_Buffer controlled_buffer_2
endmodule

module Select_b_decoder (
  input  _in0,
  input  _in1,
  input  _in2,
  input  _in3,
  input  _in4,
  input  _in5,
  input  _in6,
  input  _in7,
  output _out0,
  output _out02,
  output _out03
);

  wire and_1_out, and_2_out, and_3_out, and_4_out, and_5_out, and_6_out, and_7_out, and_8_out, and_9_out,
       not_1_out, not_2_out, not_3_out, not_4_out, not_5_out, not_6_out, not_7_out, not_8_out, not_9_out,
       not_10_out, not_11_out, not_12_out, not_13_out, not_14_out, not_15_out, not_16_out;

  not not_1 (not_1_out, _in0);
  not not_2 (not_2_out, _in1);
  and and_1 (and_1_out, not_2_out, _in3, not_3_out);
  not not_3 (not_3_out, _in5);
  and and_2 (and_2_out, _in1, not_4_out);
  not not_4 (not_4_out, _in3);
  and and_3 (and_3_out, _in1, not_5_out);
  not not_5 (not_5_out, _in4);
  not not_6 (not_6_out, _in0);
  and and_4 (and_4_out, _in3, not_7_out);
  not not_7 (not_7_out, _in5);
  and and_5 (and_5_out, _in3, _in6);
  not not_8 (not_8_out, _in0);
  and and_6 (and_6_out, not_8_out, not_9_out);
  not not_9 (not_9_out, _in1);
  not not_10 (not_10_out, _in1);
  not not_11 (not_11_out, _in3);
  and and_7 (and_7_out, not_10_out, not_11_out, not_12_out);
  not not_12 (not_12_out, _in4);
  not not_13 (not_13_out, _in1);
  and and_8 (and_8_out, not_13_out, not_14_out, _in7);
  not not_14 (not_14_out, _in4);
  not not_15 (not_15_out, _in1);
  and and_9 (and_9_out, not_15_out, _in3, not_16_out);
  not not_16 (not_16_out, _in5);
  or or_1 (_out0, not_1_out, and_1_out, _in2, and_2_out, and_3_out);
  or or_2 (_out02, not_6_out, and_4_out, and_5_out, _in1);
  or or_3 (_out03, and_6_out, and_7_out, and_8_out, and_9_out);
endmodule

module Load_decoder (
  input  _in0,
  input  _in1,
  input  _in2,
  input  _in3,
  input  _in4,
  input  _in5,
  input  _in6,
  input  _in7,
  output _out0,
  output _out02,
  output _out03
);

  wire and_1_out, and_2_out, and_3_out, and_4_out, and_5_out, and_6_out, and_7_out, and_8_out, and_9_out,
       and_10_out, and_11_out, not_1_out, not_2_out, not_3_out, not_4_out, not_5_out, not_6_out, not_7_out,
       not_8_out, not_9_out, not_10_out, not_11_out, not_12_out, not_13_out, not_14_out, not_15_out,
       not_16_out;

  and and_1 (and_1_out, _in5, not_1_out, not_2_out);
  not not_1 (not_1_out, _in6);
  not not_2 (not_2_out, _in7);
  and and_2 (and_2_out, _in0, _in3, _in5);
  not not_3 (not_3_out, _in0);
  and and_3 (and_3_out, not_3_out, _in3, not_4_out);
  not not_4 (not_4_out, _in5);
  not not_5 (not_5_out, _in0);
  and and_4 (and_4_out, not_5_out, _in3, _in7);
  not not_6 (not_6_out, _in0);
  and and_5 (and_5_out, not_6_out, _in3, _in6);
  not not_7 (not_7_out, _in5);
  and and_6 (and_6_out, _in3, not_7_out, _in6);
  not not_8 (not_8_out, _in0);
  not not_9 (not_9_out, _in6);
  not not_10 (not_10_out, _in7);
  not not_11 (not_11_out, _in3);
  not not_12 (not_12_out, _in6);
  not not_13 (not_13_out, _in7);
  not not_14 (not_14_out, _in0);
  not not_15 (not_15_out, _in3);
  not not_16 (not_16_out, _in5);
  or or_1 (_out0, and_1_out, _in2, and_2_out);
  or or_2 (_out02, and_3_out, and_4_out, and_5_out, and_6_out);
  and and_7 (and_7_out, not_8_out, _in5, not_9_out, not_10_out);
  and and_8 (and_8_out, not_11_out, _in5, not_12_out, not_13_out);
  and and_9 (and_9_out, not_14_out, _in4);
  and and_10 (and_10_out, not_15_out, _in4);
  and and_11 (and_11_out, _in0, _in3, not_16_out, _in7);
  or or_3 (_out03, and_7_out, and_8_out, and_9_out, and_10_out, and_11_out);
endmodule
