// Logisim project MicroProgramBrainfuck.circ as structural Verilog: 3 circuits, main circuit main
module main (
);

  wire button_1_out, clock_1_out, decoder_1_use_display, decoder_1_use_keyboard, decoder_2_out0,
       decoder_2_out1, decoder_2_out2, decoder_2_out3;
  wire [1:0] decoder_1_select_im, decoder_1_select_reg, decoder_1_target_reg;
  wire [2:0] rom_1_data;
  wire [6:0] bit_extender_2_out, keyboard_1_data;
  wire [7:0] adder_1_out, bit_extender_1_out, decoder_1_micro_addr, multiplexer_1_out, multiplexer_2_out,
       multiplexer_3_out, ram_1_data, register_1_q, register_2_q, register_3_q, rom_2_out_9;

  Keyboard keyboard_1 (.clk(clock_1_out), .re(decoder_1_use_keyboard), .data(keyboard_1_data));  // open: clr, avail
  ROM_part #(.dataWidth(3)) rom_1 (.addr(register_3_q), .data(rom_1_data));  // open: sel
  ROM rom_2 (
    .in_1(decoder_1_micro_addr[0]), .in_2(decoder_1_micro_addr[1]), .in_3(decoder_1_micro_addr[2]),
    .in_4(decoder_1_micro_addr[3]), .in_5(decoder_1_micro_addr[4]), .in_6(decoder_1_micro_addr[5]),
    .in_7(decoder_1_micro_addr[6]), .in_8(decoder_1_micro_addr[7]), .out_9(rom_2_out_9[0]),
    .out_10(rom_2_out_9[1]), .out_11(rom_2_out_9[2]), .out_12(rom_2_out_9[3]), .out_13(rom_2_out_9[4]),
    .out_14(rom_2_out_9[5]), .out_15(rom_2_out_9[6]), .out_16(rom_2_out_9[7]));
  decoder decoder_1 (
    .micro_code(rom_2_out_9), .bf_code(rom_1_data), .reg_c(register_2_q), .select_reg(decoder_1_select_reg),
    .select_im(decoder_1_select_im), .use_keyboard(decoder_1_use_keyboard),
    .use_display(decoder_1_use_display), .micro_addr(decoder_1_micro_addr),
    .target_reg(decoder_1_target_reg), .Clock(clock_1_out), .reset(button_1_out), .ram(ram_1_data));
  Decoder #(.select(2)) decoder_2 (
    .out0(decoder_2_out0), .out1(decoder_2_out1), .out2(decoder_2_out2), .out3(decoder_2_out3),
    .sel(decoder_1_target_reg));  // open: en
  assign bit_extender_1_out = {{1{1'b0}}, keyboard_1_data};  // Bit_Extender bit_extender_1
  Clock clock_1 (.out(clock_1_out));
  Multiplexer #(.width(8)) multiplexer_1 (
    .in0(adder_1_out), .in1(bit_extender_1_out), .out(multiplexer_1_out), .sel(decoder_1_use_keyboard));  // open: en
  Register register_1 (
    .D(multiplexer_1_out), .en(decoder_2_out0), .Q(register_1_q), .clk(clock_1_out), .clr(button_1_out));
  Register register_2 (
    .D(multiplexer_1_out), .en(decoder_2_out1), .Q(register_2_q), .clk(clock_1_out), .clr(button_1_out));
  Register register_3 (
    .D(multiplexer_1_out), .en(decoder_2_out2), .Q(register_3_q), .clk(clock_1_out), .clr(button_1_out));
  Bit_Extender #(.out_width(7)) bit_extender_2 (.in(multiplexer_1_out), .out(bit_extender_2_out));
  TTY tty_1 (.data(bit_extender_2_out), .clk(clock_1_out), .we(decoder_1_use_display), .clr(button_1_out));
  Button button_1 (.out(button_1_out));
  RAM #(.bus("separate")) ram_1 (
    .addr(register_1_q), .din(multiplexer_1_out), .data(ram_1_data), .str(decoder_2_out3), .clk(clock_1_out),
    .clr(button_1_out));  // open: sel, ld
  Multiplexer #(.select(2), .width(8)) multiplexer_2 (
    .in0(register_1_q), .in1(register_2_q), .in2(register_3_q), .in3(ram_1_data), .out(multiplexer_2_out),
    .sel(decoder_1_select_reg));  // open: en
  Multiplexer #(.select(2), .width(8)) multiplexer_3 (
    .in0({8{1'b0}}), .in1({8{1'b1}}), .in2(8'h1), .out(multiplexer_3_out), .sel(decoder_1_select_im));  // open: in3, en
  Adder adder_1 (.a(multiplexer_2_out), .b(multiplexer_3_out), .out(adder_1_out));  // open: cin, cout

  // Notes on the sheet:
  //   contents of rom_1 (hex, n*v repeats v):
  //   0 9*2 6 1 8*2 0 3 7 1 4 0 7*2 6 1 4*2 0 3 7 1 2 4 7*2 4 4 2 2 2 4 6 3 7 0 8*2 6 1 4*2 0 3 7 1 4 0
  //   11*2 6 1 5*2 0 3 7 1 4 0 8*2 6 1 2 2 2 0 3 7 1 4 2 2 2 4 6*3 4 8*3 4 6 3 7 0 8*2 6 1 4*2 0 3 7 1 2 4
  //   6 3 7 10*2 4 2 6 7
endmodule

// DECODER
module decoder (
  input  [2:0] bf_code,
  input  [7:0] micro_code,
  input  [7:0] reg_c,
  input  [7:0] ram,
  input  Clock,
  input  reset,
  output [1:0] select_reg,
  output [1:0] select_im,
  output [1:0] target_reg,
  output use_keyboard,
  output use_display,
  output [7:0] micro_addr
);

  wire and_1_out, and_2_out, and_3_out, and_4_out, and_7_out, and_8_out, and_9_out, and_10_out, and_11_out,
       and_12_out, not_1_out, not_2_out, not_3_out, not_4_out, not_5_out, not_6_out, not_7_out, not_8_out,
       not_9_out, not_10_out, not_11_out, not_12_out, not_13_out, not_14_out, not_15_out, not_16_out,
       not_17_out, not_18_out, not_19_out, not_20_out, not_21_out, not_22_out, not_23_out, not_24_out,
       not_25_out, not_26_out, not_27_out, not_28_out, or_1_out, or_2_out, or_3_out, or_4_out;
  wire [7:0] adder_1_out, bit_extender_1_out, multiplexer_1_out, multiplexer_2_out, multiplexer_6_out;

  not not_1 (not_1_out, bf_code[0]);
  and and_1 (and_1_out, not_1_out, bf_code[1], bf_code[2]);
  and and_2 (and_2_out, bf_code[0], bf_code[1], bf_code[2]);
  or or_1 (or_1_out, reg_c[0], reg_c[1], reg_c[2], reg_c[3], reg_c[4], reg_c[5], reg_c[6], reg_c[7]);
  or or_2 (or_2_out, ram[0], ram[1], ram[2], ram[3], ram[4], ram[5], ram[6], ram[7]);
  not not_2 (not_2_out, and_1_out);
  not not_3 (not_3_out, and_2_out);
  not not_4 (not_4_out, micro_code[6]);
  not not_5 (not_5_out, micro_code[7]);
  not not_6 (not_6_out, micro_code[4]);
  not not_7 (not_7_out, micro_code[5]);
  not not_8 (not_8_out, micro_code[7]);
  not not_9 (not_9_out, micro_code[5]);
  not not_10 (not_10_out, micro_code[7]);
  not not_11 (not_11_out, micro_code[4]);
  not not_12 (not_12_out, micro_code[7]);
  not not_13 (not_13_out, micro_code[7]);
  not not_14 (not_14_out, micro_code[4]);
  not not_15 (not_15_out, micro_code[5]);
  not not_16 (not_16_out, micro_code[6]);
  not not_17 (not_17_out, micro_code[4]);
  not not_18 (not_18_out, micro_code[6]);
  not not_19 (not_19_out, micro_code[7]);
  not not_20 (not_20_out, micro_code[5]);
  not not_21 (not_21_out, micro_code[6]);
  not not_22 (not_22_out, micro_code[7]);
  not not_23 (not_23_out, micro_code[4]);
  not not_24 (not_24_out, micro_code[6]);
  not not_25 (not_25_out, micro_code[7]);
  not not_26 (not_26_out, micro_code[5]);
  not not_27 (not_27_out, micro_code[6]);
  not not_28 (not_28_out, micro_code[7]);
  and and_3 (and_3_out, not_17_out, micro_code[5], not_18_out, not_19_out);
  or or_3 (or_3_out, and_3_out, and_4_out);
  and and_4 (and_4_out, not_20_out, not_21_out, not_22_out);
  and and_5 (use_keyboard, not_23_out, micro_code[5], not_24_out, not_25_out);
  and and_6 (use_display, micro_code[4], not_26_out, not_27_out, not_28_out);
  and and_7 (and_7_out, or_2_out, micro_code[4], micro_code[5], not_4_out, not_5_out);
  and and_8 (and_8_out, not_2_out, not_6_out, not_7_out, micro_code[6], not_8_out);
  or or_4 (or_4_out, and_7_out, and_8_out, and_9_out, and_10_out, and_11_out);
  and and_9 (and_9_out, not_3_out, micro_code[4], not_9_out, micro_code[6], not_10_out);
  and and_10 (and_10_out, or_1_out, not_11_out, micro_code[5], micro_code[6], not_12_out);
  and and_11 (and_11_out, micro_code[4], micro_code[5], micro_code[6], not_13_out);
  Adder adder_1 (.a(micro_addr), .b(8'h1), .out(adder_1_out));  // open: cin, cout
  assign bit_extender_1_out = {{3{1'b0}}, {micro_code[3:0], 1'b0}};  // Bit_Extender bit_extender_1
  and and_12 (and_12_out, not_14_out, not_15_out, not_16_out, micro_code[7]);
  Multiplexer #(.width(8)) multiplexer_1 (
    .in0(adder_1_out), .in1(bit_extender_1_out), .out(multiplexer_1_out), .sel(or_4_out));  // open: en
  Multiplexer #(.select(3), .width(8)) multiplexer_2 (
    .in0(8'h1c), .in1(8'h1e), .in2(8'h18), .in3(8'h1a), .in4(8'h22), .in5(8'h20), .in6(8'h4), .in7(8'he),
    .out(multiplexer_2_out), .sel(bf_code));  // open: en
  Multiplexer #(.width(2)) multiplexer_3 (
    .in0(2'b00), .in1(micro_code[3:2]), .out(select_reg), .sel(or_3_out));  // open: en
  Multiplexer #(.width(2)) multiplexer_4 (
    .in0(2'b00), .in1(micro_code[1:0]), .out(select_im), .sel(or_3_out));  // open: en
  Multiplexer #(.width(2)) multiplexer_5 (
    .in0(2'b00), .in1(micro_code[3:2]), .out(target_reg), .sel(or_3_out));  // open: en
  Register register_1 (.D(multiplexer_6_out), .en(1'b1), .Q(micro_addr), .clk(Clock), .clr(reset));
  Multiplexer #(.width(8)) multiplexer_6 (
    .in0(multiplexer_1_out), .in1(multiplexer_2_out), .out(multiplexer_6_out), .sel(and_12_out));  // open: en

  // Notes on the sheet:
  //   code!=[
  //   code!=]
  //   reg_c!= 0
  //   ram !=0
  //   jump
  //   XXXX
endmodule

// PGM ROM
module ROM (
  input  in_1,
  input  in_2,
  input  in_3,
  input  in_4,
  input  in_5,
  input  in_6,
  input  in_7,
  input  in_8,
  output out_9,
  output out_10,
  output out_11,
  output out_12,
  output out_13,
  output out_14,
  output out_15,
  output out_16
);

  ROM_part rom_1 (
    .addr({in_8, in_7, in_6, in_5, in_4, in_3, in_2, in_1}),
    .data({out_16, out_15, out_14, out_13, out_12, out_11, out_10, out_9}));  // open: sel

  // Notes on the sheet:
  //   contents of rom_1 (hex, n*v repeats v):
  //   80 0 a 70 31 6 a 0 45 6 56 5 63 71 5 0 9 0 4a 6 5b 5 68 70 e 71 d 71 2 71 1 71 2c 71 1c 71
endmodule
