// Logisim project LifeGame.circ as structural Verilog: 5 circuits, main circuit main
module main (
  input  in_1,
  input  [7:0] in_2,
  input  [7:0] in_3,
  input  [7:0] in_4,
  input  [7:0] in_5,
  input  [7:0] in_6,
  input  [7:0] in_7,
  input  [7:0] in_8,
  input  [7:0] in_9
);

  wire clock_1_out;
  wire [7:0] a, b, c, d, e, f, g, h, lg_1_out_4, lg_2_out_4, lg_3_out_4, lg_4_out_4, lg_5_out_4, lg_6_out_4,
       lg_7_out_4, lg_8_out_4, register_1_q, register_2_q, register_3_q, register_4_q, register_5_q,
       register_6_q, register_7_q, register_8_q;

  Clock clock_1 (.out(clock_1_out));
  Register register_1 (.D(a), .Q(register_1_q), .clk(clock_1_out));  // open: en, clr
  Register register_2 (.D(b), .Q(register_2_q), .clk(clock_1_out));  // open: en, clr
  Register register_3 (.D(c), .Q(register_3_q), .clk(clock_1_out));  // open: en, clr
  Register register_4 (.D(d), .Q(register_4_q), .clk(clock_1_out));  // open: en, clr
  Register register_5 (.D(e), .Q(register_5_q), .clk(clock_1_out));  // open: en, clr
  Register register_6 (.D(f), .Q(register_6_q), .clk(clock_1_out));  // open: en, clr
  Register register_7 (.D(g), .Q(register_7_q), .clk(clock_1_out));  // open: en, clr
  Register register_8 (.D(h), .Q(register_8_q), .clk(clock_1_out));  // open: en, clr
  LG lg_1 (.in_1(register_8_q), .in_2(register_1_q), .in_3(register_2_q), .out_4(lg_1_out_4));
  LG lg_2 (.in_1(register_1_q), .in_2(register_2_q), .in_3(register_3_q), .out_4(lg_2_out_4));
  LG lg_3 (.in_1(register_2_q), .in_2(register_3_q), .in_3(register_4_q), .out_4(lg_3_out_4));
  LG lg_4 (.in_1(register_3_q), .in_2(register_4_q), .in_3(register_5_q), .out_4(lg_4_out_4));
  LG lg_5 (.in_1(register_4_q), .in_2(register_5_q), .in_3(register_6_q), .out_4(lg_5_out_4));
  LG lg_6 (.in_1(register_5_q), .in_2(register_6_q), .in_3(register_7_q), .out_4(lg_6_out_4));
  LG lg_7 (.in_1(register_6_q), .in_2(register_7_q), .in_3(register_8_q), .out_4(lg_7_out_4));
  LG lg_8 (.in_1(register_7_q), .in_2(register_8_q), .in_3(register_1_q), .out_4(lg_8_out_4));
  DotMatrix #(.matrixcols(8), .matrixrows(8)) dotmatrix_1 (
    .col0(a), .col1(b), .col2(c), .col3(d), .col4(e), .col5(f), .col6(g), .col7(h));
  Multiplexer #(.width(8)) multiplexer_1 (.in0(in_2), .in1(lg_1_out_4), .out(a), .sel(in_1));  // open: en
  Multiplexer #(.width(8)) multiplexer_2 (.in0(in_3), .in1(lg_2_out_4), .out(b), .sel(in_1));  // open: en
  Multiplexer #(.width(8)) multiplexer_3 (.in0(in_4), .in1(lg_3_out_4), .out(c), .sel(in_1));  // open: en
  Multiplexer #(.width(8)) multiplexer_4 (.in0(in_5), .in1(lg_4_out_4), .out(d), .sel(in_1));  // open: en
  Multiplexer #(.width(8)) multiplexer_5 (.in0(in_6), .in1(lg_5_out_4), .out(e), .sel(in_1));  // open: en
  Multiplexer #(.width(8)) multiplexer_6 (.in0(in_7), .in1(lg_6_out_4), .out(f), .sel(in_1));  // open: en
  Multiplexer #(.width(8)) multiplexer_7 (.in0(in_8), .in1(lg_7_out_4), .out(g), .sel(in_1));  // open: en
  Multiplexer #(.width(8)) multiplexer_8 (.in0(in_9), .in1(lg_8_out_4), .out(h), .sel(in_1));  // open: en
endmodule

module LG (
  input  [7:0] in_1,
  input  [7:0] in_2,
  input  [7:0] in_3,
  output [7:0] out_4
);

  min min_1 (.a(in_3), .b(in_2), .c(in_1), .k(3'b000), .o(out_4[0]));
  min min_2 (.a(in_3), .b(in_2), .c(in_1), .k(3'b001), .o(out_4[1]));
  min min_3 (.a(in_3), .b(in_2), .c(in_1), .k(3'b010), .o(out_4[2]));
  min min_4 (.a(in_3), .b(in_2), .c(in_1), .k(3'b011), .o(out_4[3]));
  min min_5 (.a(in_3), .b(in_2), .c(in_1), .k(3'b100), .o(out_4[4]));
  min min_6 (.a(in_3), .b(in_2), .c(in_1), .k(3'b101), .o(out_4[5]));
  min min_7 (.a(in_3), .b(in_2), .c(in_1), .k(3'b110), .o(out_4[6]));
  min min_8 (.a(in_3), .b(in_2), .c(in_1), .k(3'b111), .o(out_4[7]));
endmodule

module NearSelecter (
  input  [7:0] in_1,
  input  [7:0] in_2,
  input  [7:0] in_3,
  input  [2:0] in_4,
  output out_5,
  output out_6,
  output out_7,
  output out_8,
  output center,
  output out_10,
  output out_11,
  output out_12,
  output out_13
);

  wire [2:0] adder_1_out, adder_2_out, adder_3_out, adder_4_out, adder_5_out, adder_6_out, adder_7_out,
       adder_8_out, adder_9_out;

  Adder #(.width(3)) adder_1 (.a(in_4), .b(3'b111), .out(adder_1_out));  // open: cin, cout
  Adder #(.width(3)) adder_2 (.a(in_4), .b(3'b111), .out(adder_2_out));  // open: cin, cout
  Adder #(.width(3)) adder_3 (.a(in_4), .b(3'b111), .out(adder_3_out));  // open: cin, cout
  Adder #(.width(3)) adder_4 (.a(in_4), .b(3'b000), .out(adder_4_out));  // open: cin, cout
  Adder #(.width(3)) adder_5 (.a(in_4), .b(3'b000), .out(adder_5_out));  // open: cin, cout
  Adder #(.width(3)) adder_6 (.a(in_4), .b(3'b000), .out(adder_6_out));  // open: cin, cout
  Adder #(.width(3)) adder_7 (.a(in_4), .b(3'b001), .out(adder_7_out));  // open: cin, cout
  Adder #(.width(3)) adder_8 (.a(in_4), .b(3'b001), .out(adder_8_out));  // open: cin, cout
  Adder #(.width(3)) adder_9 (.a(in_4), .b(3'b001), .out(adder_9_out));  // open: cin, cout
  Multiplexer #(.select(3)) multiplexer_1 (
    .in0(in_1[0]), .in1(in_1[1]), .in2(in_1[2]), .in3(in_1[3]), .in4(in_1[4]), .in5(in_1[5]), .in6(in_1[6]),
    .in7(in_1[7]), .out(out_5), .sel(adder_1_out));  // open: en
  Multiplexer #(.select(3)) multiplexer_2 (
    .in0(in_2[0]), .in1(in_2[1]), .in2(in_2[2]), .in3(in_2[3]), .in4(in_2[4]), .in5(in_2[5]), .in6(in_2[6]),
    .in7(in_2[7]), .out(out_6), .sel(adder_2_out));  // open: en
  Multiplexer #(.select(3)) multiplexer_3 (
    .in0(in_3[0]), .in1(in_3[1]), .in2(in_3[2]), .in3(in_3[3]), .in4(in_3[4]), .in5(in_3[5]), .in6(in_3[6]),
    .in7(in_3[7]), .out(out_7), .sel(adder_3_out));  // open: en
  Multiplexer #(.select(3)) multiplexer_4 (
    .in0(in_1[0]), .in1(in_1[1]), .in2(in_1[2]), .in3(in_1[3]), .in4(in_1[4]), .in5(in_1[5]), .in6(in_1[6]),
    .in7(in_1[7]), .out(out_8), .sel(adder_4_out));  // open: en
  Multiplexer #(.select(3)) multiplexer_5 (
    .in0(in_2[0]), .in1(in_2[1]), .in2(in_2[2]), .in3(in_2[3]), .in4(in_2[4]), .in5(in_2[5]), .in6(in_2[6]),
    .in7(in_2[7]), .out(center), .sel(adder_5_out));  // open: en
  Multiplexer #(.select(3)) multiplexer_6 (
    .in0(in_3[0]), .in1(in_3[1]), .in2(in_3[2]), .in3(in_3[3]), .in4(in_3[4]), .in5(in_3[5]), .in6(in_3[6]),
    .in7(in_3[7]), .out(out_10), .sel(adder_6_out));  // open: en
  Multiplexer #(.select(3)) multiplexer_7 (
    .in0(in_1[0]), .in1(in_1[1]), .in2(in_1[2]), .in3(in_1[3]), .in4(in_1[4]), .in5(in_1[5]), .in6(in_1[6]),
    .in7(in_1[7]), .out(out_11), .sel(adder_7_out));  // open: en
  Multiplexer #(.select(3)) multiplexer_8 (
    .in0(in_2[0]), .in1(in_2[1]), .in2(in_2[2]), .in3(in_2[3]), .in4(in_2[4]), .in5(in_2[5]), .in6(in_2[6]),
    .in7(in_2[7]), .out(out_12), .sel(adder_8_out));  // open: en
  Multiplexer #(.select(3)) multiplexer_9 (
    .in0(in_3[0]), .in1(in_3[1]), .in2(in_3[2]), .in3(in_3[3]), .in4(in_3[4]), .in5(in_3[5]), .in6(in_3[6]),
    .in7(in_3[7]), .out(out_13), .sel(adder_9_out));  // open: en
endmodule

module count1 (
  input  in_1,
  input  in_2,
  input  in_3,
  input  in_4,
  input  in_5,
  input  in_6,
  input  in_7,
  input  in_8,
  output [2:0] out_9
);

  wire [2:0] adder_1_out, adder_2_out, adder_3_out, adder_4_out, adder_5_out, adder_6_out,
       bit_extender_1_out, bit_extender_2_out, bit_extender_3_out, bit_extender_4_out, bit_extender_5_out,
       bit_extender_6_out, bit_extender_7_out, bit_extender_8_out;

  assign bit_extender_1_out = {{2{1'b0}}, in_1};  // Bit_Extender bit_extender_1
  assign bit_extender_2_out = {{2{1'b0}}, in_2};  // Bit_Extender bit_extender_2
  assign bit_extender_3_out = {{2{1'b0}}, in_3};  // Bit_Extender bit_extender_3
  assign bit_extender_4_out = {{2{1'b0}}, in_4};  // Bit_Extender bit_extender_4
  assign bit_extender_5_out = {{2{1'b0}}, in_5};  // Bit_Extender bit_extender_5
  assign bit_extender_6_out = {{2{1'b0}}, in_6};  // Bit_Extender bit_extender_6
  assign bit_extender_7_out = {{2{1'b0}}, in_7};  // Bit_Extender bit_extender_7
  assign bit_extender_8_out = {{2{1'b0}}, in_8};  // Bit_Extender bit_extender_8
  Adder #(.width(3)) adder_1 (.a(bit_extender_1_out), .b(bit_extender_2_out), .out(adder_1_out));  // open: cin, cout
  Adder #(.width(3)) adder_2 (.a(bit_extender_3_out), .b(bit_extender_4_out), .out(adder_2_out));  // open: cin, cout
  Adder #(.width(3)) adder_3 (.a(bit_extender_5_out), .b(bit_extender_6_out), .out(adder_3_out));  // open: cin, cout
  Adder #(.width(3)) adder_4 (.a(bit_extender_7_out), .b(bit_extender_8_out), .out(adder_4_out));  // open: cin, cout
  Adder #(.width(3)) adder_5 (.a(adder_1_out), .b(adder_2_out), .out(adder_5_out));  // open: cin, cout
  Adder #(.width(3)) adder_6 (.a(adder_3_out), .b(adder_4_out), .out(adder_6_out));  // open: cin, cout
  Adder #(.width(3)) adder_7 (.a(adder_5_out), .b(adder_6_out), .out(out_9));  // open: cin, cout
endmodule

module min (
  input  [7:0] a,
  input  [7:0] b,
  input  [7:0] c,
  input  [2:0] k,
  output o
);

  wire and_1_out, and_2_out, and_3_out, nearselecter_1_center, nearselecter_1_out_5, nearselecter_1_out_6,
       nearselecter_1_out_7, nearselecter_1_out_8, nearselecter_1_out_10, nearselecter_1_out_11,
       nearselecter_1_out_12, nearselecter_1_out_13, not_1_out, not_2_out, not_3_out, not_4_out, not_5_out,
       or_1_out;
  wire [2:0] count1_1_out_9;

  NearSelecter nearselecter_1 (
    .in_1(a), .in_2(b), .in_3(c), .in_4(k), .out_5(nearselecter_1_out_5), .out_6(nearselecter_1_out_6),
    .out_7(nearselecter_1_out_7), .out_8(nearselecter_1_out_8), .center(nearselecter_1_center),
    .out_10(nearselecter_1_out_10), .out_11(nearselecter_1_out_11), .out_12(nearselecter_1_out_12),
    .out_13(nearselecter_1_out_13));
  count1 count1_1 (
    .in_1(nearselecter_1_out_5), .in_2(nearselecter_1_out_6), .in_3(nearselecter_1_out_7),
    .in_4(nearselecter_1_out_8), .in_5(nearselecter_1_out_10), .in_6(nearselecter_1_out_11),
    .in_7(nearselecter_1_out_12), .in_8(nearselecter_1_out_13), .out_9(count1_1_out_9));
  not not_1 (not_1_out, count1_1_out_9[2]);
  not not_2 (not_2_out, nearselecter_1_center);
  not not_3 (not_3_out, count1_1_out_9[2]);
  not not_4 (not_4_out, count1_1_out_9[0]);
  not not_5 (not_5_out, count1_1_out_9[2]);
  and and_1 (and_1_out, count1_1_out_9[0], count1_1_out_9[1], not_1_out);
  assign o = not_2_out ? and_1_out : 1'bz;  // Controlled_Buffer controlled_buffer_1
  and and_2 (and_2_out, count1_1_out_9[0], count1_1_out_9[1], not_3_out);
  and and_3 (and_3_out, not_4_out, count1_1_out_9[1], not_5_out);
  or or_1 (or_1_out, and_2_out, and_3_out);
  assign o = nearselecter_1_center ? or_1_out : 1'bz;  // Controlled_Buffer controlled_buffer_2
endmodule
