// Logisim project display.circ as structural Verilog: 3 circuits, main circuit main
module main (
  input  [31:0] in_1,
  input  [4:0] in_2,
  input  in_3
);

  wire clock_1_out;
  wire [31:0] uu_1__0, uu_1__1, uu_1__2, uu_1__3, uu_1__4, uu_1__5, uu_1__6, uu_1__7, uu_1__8, uu_1__9,
       uu_1__10, uu_1__11, uu_1__12, uu_1__13, uu_1__14, uu_1__16, uu_1__17, uu_1__18, uu_1__19, uu_1__20,
       uu_1__21, uu_1__22, uu_1__23, uu_1__24, uu_1__25, uu_1__26, uu_1__27, uu_1__28, uu_1__29, uu_1__30,
       uu_1__31, uu_1_out_33;

  DotMatrix #(.matrixcols(32), .matrixrows(32)) dotmatrix_1 (
    .col0(uu_1__0), .col1(uu_1__1), .col2(uu_1__2), .col3(uu_1__3), .col4(uu_1__4), .col5(uu_1__5),
    .col6(uu_1__6), .col7(uu_1__7), .col8(uu_1__8), .col9(uu_1__9), .col10(uu_1__10), .col11(uu_1__11),
    .col12(uu_1__12), .col13(uu_1__13), .col14(uu_1__14), .col15(uu_1_out_33), .col16(uu_1__16),
    .col17(uu_1__17), .col18(uu_1__18), .col19(uu_1__19), .col20(uu_1__20), .col21(uu_1__21),
    .col22(uu_1__22), .col23(uu_1__23), .col24(uu_1__24), .col25(uu_1__25), .col26(uu_1__26),
    .col27(uu_1__27), .col28(uu_1__28), .col29(uu_1__29), .col30(uu_1__30), .col31(uu_1__31));
  uu uu_1 (
    .in_1(in_1), .clk(clock_1_out), .address(in_2), ._0(uu_1__0), ._1(uu_1__1), ._2(uu_1__2), ._16(uu_1__16),
    ._3(uu_1__3), ._17(uu_1__17), ._4(uu_1__4), ._18(uu_1__18), ._5(uu_1__5), ._19(uu_1__19), ._6(uu_1__6),
    ._20(uu_1__20), ._7(uu_1__7), ._21(uu_1__21), ._8(uu_1__8), ._22(uu_1__22), ._9(uu_1__9), ._23(uu_1__23),
    ._10(uu_1__10), ._24(uu_1__24), ._11(uu_1__11), ._25(uu_1__25), ._12(uu_1__12), ._26(uu_1__26),
    ._13(uu_1__13), ._27(uu_1__27), ._14(uu_1__14), ._28(uu_1__28), .out_33(uu_1_out_33), ._29(uu_1__29),
    ._30(uu_1__30), ._31(uu_1__31), ._1_Update_0_Hold(in_3));
  Clock clock_1 (.out(clock_1_out));
endmodule

module uu (
  input  [31:0] in_1,
  input  clk,
  input  _1_Update_0_Hold,
  input  [4:0] address,
  output [31:0] _0,
  output [31:0] _1,
  output [31:0] _2,
  output [31:0] _16,
  output [31:0] _3,
  output [31:0] _17,
  output [31:0] _4,
  output [31:0] _18,
  output [31:0] _5,
  output [31:0] _19,
  output [31:0] _6,
  output [31:0] _20,
  output [31:0] _7,
  output [31:0] _21,
  output [31:0] _8,
  output [31:0] _22,
  output [31:0] _9,
  output [31:0] _23,
  output [31:0] _10,
  output [31:0] _24,
  output [31:0] _11,
  output [31:0] _25,
  output [31:0] _12,
  output [31:0] _26,
  output [31:0] _13,
  output [31:0] _27,
  output [31:0] _14,
  output [31:0] _28,
  output [31:0] out_33,
  output [31:0] _29,
  output [31:0] _30,
  output [31:0] _31
);

  wire decoder_1_out0, decoder_1_out1, decoder_1_out2, decoder_1_out3, decoder_2_out0, decoder_2_out1,
       decoder_2_out2, decoder_2_out3, decoder_2_out4, decoder_2_out5, decoder_2_out6, decoder_2_out7,
       decoder_3_out0, decoder_3_out1, decoder_3_out2, decoder_3_out3, decoder_3_out4, decoder_3_out5,
       decoder_3_out6, decoder_3_out7, decoder_4_out0, decoder_4_out1, decoder_4_out2, decoder_4_out3,
       decoder_4_out4, decoder_4_out5, decoder_4_out6, decoder_4_out7, decoder_5_out0, decoder_5_out1,
       decoder_5_out2, decoder_5_out3, decoder_5_out4, decoder_5_out5, decoder_5_out6, decoder_5_out7;

  Decoder #(.select(2), .disabled(0)) decoder_1 (
    .out0(decoder_1_out0), .out1(decoder_1_out1), .out2(decoder_1_out2), .out3(decoder_1_out3),
    .sel(address[4:3]), .en(_1_Update_0_Hold));
  Decoder #(.select(3), .disabled(0)) decoder_2 (
    .out0(decoder_2_out0), .out1(decoder_2_out1), .out2(decoder_2_out2), .out3(decoder_2_out3),
    .out4(decoder_2_out4), .out5(decoder_2_out5), .out6(decoder_2_out6), .out7(decoder_2_out7),
    .sel(address[2:0]), .en(decoder_1_out0));
  Decoder #(.select(3), .disabled(0)) decoder_3 (
    .out0(decoder_3_out0), .out1(decoder_3_out1), .out2(decoder_3_out2), .out3(decoder_3_out3),
    .out4(decoder_3_out4), .out5(decoder_3_out5), .out6(decoder_3_out6), .out7(decoder_3_out7),
    .sel(address[2:0]), .en(decoder_1_out1));
  Decoder #(.select(3), .disabled(0)) decoder_4 (
    .out0(decoder_4_out0), .out1(decoder_4_out1), .out2(decoder_4_out2), .out3(decoder_4_out3),
    .out4(decoder_4_out4), .out5(decoder_4_out5), .out6(decoder_4_out6), .out7(decoder_4_out7),
    .sel(address[2:0]), .en(decoder_1_out2));
  Decoder #(.select(3), .disabled(0)) decoder_5 (
    .out0(decoder_5_out0), .out1(decoder_5_out1), .out2(decoder_5_out2), .out3(decoder_5_out3),
    .out4(decoder_5_out4), .out5(decoder_5_out5), .out6(decoder_5_out6), .out7(decoder_5_out7),
    .sel(address[2:0]), .en(decoder_1_out3));
  aa aa_1 (
    .in_1(in_1), .clk(clk), ._1(decoder_2_out0), ._2(decoder_2_out1), ._3(decoder_2_out2),
    ._4(decoder_2_out3), ._5(decoder_2_out4), ._6(decoder_2_out5), ._7(decoder_2_out6), ._8(decoder_2_out7),
    ._1_2(_0), ._2_2(_1), ._3_2(_2), ._4_2(_3), ._5_2(_4), ._6_2(_5), ._7_2(_6), ._8_2(_7));
  aa aa_2 (
    .in_1(in_1), .clk(clk), ._1(decoder_3_out0), ._2(decoder_3_out1), ._3(decoder_3_out2),
    ._4(decoder_3_out3), ._5(decoder_3_out4), ._6(decoder_3_out5), ._7(decoder_3_out6), ._8(decoder_3_out7),
    ._1_2(_8), ._2_2(_9), ._3_2(_10), ._4_2(_11), ._5_2(_12), ._6_2(_13), ._7_2(_14), ._8_2(out_33));
  aa aa_3 (
    .in_1(in_1), .clk(clk), ._1(decoder_4_out0), ._2(decoder_4_out1), ._3(decoder_4_out2),
    ._4(decoder_4_out3), ._5(decoder_4_out4), ._6(decoder_4_out5), ._7(decoder_4_out6), ._8(decoder_4_out7),
    ._1_2(_16), ._2_2(_17), ._3_2(_18), ._4_2(_19), ._5_2(_20), ._6_2(_21), ._7_2(_22), ._8_2(_23));
  aa aa_4 (
    .in_1(in_1), .clk(clk), ._1(decoder_5_out0), ._2(decoder_5_out1), ._3(decoder_5_out2),
    ._4(decoder_5_out3), ._5(decoder_5_out4), ._6(decoder_5_out5), ._7(decoder_5_out6), ._8(decoder_5_out7),
    ._1_2(_24), ._2_2(_25), ._3_2(_26), ._4_2(_27), ._5_2(_28), ._6_2(_29), ._7_2(_30), ._8_2(_31));
endmodule

module aa (
  input  [31:0] in_1,
  input  clk,
  input  _1,
  input  _2,
  input  _3,
  input  _4,
  input  _5,
  input  _6,
  input  _7,
  input  _8,
  output [31:0] _1_2,
  output [31:0] _2_2,
  output [31:0] _3_2,
  output [31:0] _4_2,
  output [31:0] _5_2,
  output [31:0] _6_2,
  output [31:0] _7_2,
  output [31:0] _8_2
);

  Register #(.width(32)) register_1 (.D(in_1), .en(_1), .Q(_1_2), .clk(clk));  // open: clr
  Register #(.width(32)) register_2 (.D(in_1), .en(_2), .Q(_2_2), .clk(clk));  // open: clr
  Register #(.width(32)) register_3 (.D(in_1), .en(_3), .Q(_3_2), .clk(clk));  // open: clr
  Register #(.width(32)) register_4 (.D(in_1), .en(_4), .Q(_4_2), .clk(clk));  // open: clr
  Register #(.width(32)) register_5 (.D(in_1), .en(_5), .Q(_5_2), .clk(clk));  // open: clr
  Register #(.width(32)) register_6 (.D(in_1), .en(_6), .Q(_6_2), .clk(clk));  // open: clr
  Register #(.width(32)) register_7 (.D(in_1), .en(_7), .Q(_7_2), .clk(clk));  // open: clr
  Register #(.width(32)) register_8 (.D(in_1), .en(_8), .Q(_8_2), .clk(clk));  // open: clr
endmodule
